// Logisim project ex_02_converter_binario_gray.circ as structural Verilog
module main (
  input  [3:0] Bin_in,
  output [3:0] Gray_out,
  output [3:0] Gray_out_vhdl
);

  // Probe on Bin_in
  // Probe on Gray_out_vhdl
  xor xor_1 (Gray_out[2], Bin_in[3], Bin_in[2]);
  xor xor_2 (Gray_out[1], Bin_in[2], Bin_in[1]);
  xor xor_3 (Gray_out[0], Bin_in[1], Bin_in[0]);
  Conv_bin_gray conv_bin_gray_1 (.bin_i(Bin_in), .gray_o(Gray_out_vhdl));

  assign Gray_out[3] = Bin_in[3];

  // Other names for the same wires on the sheet: G_o[3:0] = Gray_out_vhdl
endmodule

// VHDL entity Conv_bin_gray, as the project stores it:
--------------------------------------------------------------------------------
-- Project :
-- File    :
-- Autor   :
-- Date    :
--
--------------------------------------------------------------------------------
-- Description :
--
--------------------------------------------------------------------------------

LIBRARY ieee;
USE ieee.std_logic_1164.all;

ENTITY Conv_bin_gray IS
  PORT (
  ------------------------------------------------------------------------------
  --Insert input ports below
    bin_i        : IN  std_logic_vector(3 DOWNTO 0); -- input vector example
  ------------------------------------------------------------------------------
  --Insert output ports below
    gray_o        : OUT std_logic_vector(3 DOWNTO 0)  -- output vector example
    );
END Conv_bin_gray;

--------------------------------------------------------------------------------
--Complete your VHDL description below
--------------------------------------------------------------------------------

ARCHITECTURE TypeArchitecture OF Conv_bin_gray IS

BEGIN

	gray_o(3) <= bin_i(3);
	gray_o(2) <= bin_i(3) XOR bin_i(2);
	gray_o(1) <= bin_i(2) XOR bin_i(1);
	gray_o(0) <= bin_i(1) XOR bin_i(0);

END TypeArchitecture;
