// Logisim project 01_tutorial_logisim.circ as structural Verilog: 1 circuit, main circuit main
module main (
  input  X,
  input  Y,
  output o
);

  wire And1_out, And2_out, not_1_out, not_2_out;

  not not_1 (not_1_out, Y);
  not not_2 (not_2_out, X);
  and And1 (And1_out, X, not_1_out);
  and And2 (And2_out, not_2_out, Y);
  or Or1 (o, And1_out, And2_out);
endmodule
