// Logisim project ex1.circ as structural Verilog
module main (
  input  X,
  input  Y,
  output A1,
  output A2,
  output D2,
  output D1,
  output A1_v,
  output A2_v,
  output D1_v,
  output D2_v
);

  wire not_1_out, not_2_out, not_3_out, not_4_out;

  nor nor_1 (A1, X, Y);
  nand nand_1 (D1, X, Y);
  Exercicio_01 exercicio_01_1 (.X(X), .Y(Y), .A1(A1_v), .A2(A2_v), .D1(D1_v), .D2(D2_v));
  not not_1 (not_1_out, X);
  not not_2 (not_2_out, Y);
  not not_3 (not_3_out, X);
  not not_4 (not_4_out, Y);
  and and_1 (A2, not_1_out, not_2_out);
  or or_1 (D2, not_3_out, not_4_out);

  // Other names for the same wires on the sheet: X_tunel = X; Y_tunel = Y
endmodule

// VHDL entity Exercicio_01, as the project stores it:
--------------------------------------------------------------------------------
-- Project :
-- File    :
-- Autor   :
-- Date    :
--
--------------------------------------------------------------------------------
-- Description :
--
--------------------------------------------------------------------------------

LIBRARY ieee;
USE ieee.std_logic_1164.all;

ENTITY Exercicio_01 IS
  PORT (
  ------------------------------------------------------------------------------
  --Insert input ports below
    X        : IN  std_logic;                    -- input bit example
    Y        : IN  std_logic;                    -- input vector example
  ------------------------------------------------------------------------------
  --Insert output ports below
    A1 	   : OUT std_logic;                    -- output bit example
    A2 	   : OUT std_logic;                    -- output bit example
    D1 	   : OUT std_logic;                    -- output bit example
    D2 	   : OUT std_logic                     -- output bit example
    );
END Exercicio_01;

--------------------------------------------------------------------------------
--Complete your VHDL description below
--------------------------------------------------------------------------------

ARCHITECTURE TypeArchitecture OF Exercicio_01 IS

BEGIN

    A1 <= not (X or Y);
    A2 <= (not X) and (not Y);
    D1 <= not (X and Y);
    D2 <= (not X) or (not Y);

END TypeArchitecture;
