// Logisim project Ex2_c.circ as structural Verilog
module main (
  input  A,
  input  B,
  input  C,
  input  D,
  output Z,
  output Z_VHDL
);

  wire AND1_out, AND2_out, AND3_out, not_1_out, not_2_out, not_3_out;

  not not_1 (not_1_out, A);
  not not_2 (not_2_out, B);
  not not_3 (not_3_out, C);
  and AND1 (AND1_out, not_1_out, not_2_out, not_3_out);
  and AND2 (AND2_out, A, not_2_out, not_3_out);
  and AND3 (AND3_out, not_1_out, not_2_out, D);
  Ex2c_VHDL ex2c_vhdl_1 (.A(A), .B(B), .C(C), .D(D), .Z(Z_VHDL));
  or or_1 (Z, AND1_out, AND2_out, AND3_out);

  // Other names for the same wires on the sheet: A_tunel = A; B_tunel = B; C_tunel = C; D_tunel = D
endmodule

// VHDL entity Ex2c_VHDL, as the project stores it:
--------------------------------------------------------------------------------
-- Project :
-- File    :
-- Autor   :
-- Date    :
--
--------------------------------------------------------------------------------
-- Description :
--
--------------------------------------------------------------------------------

LIBRARY ieee;
USE ieee.std_logic_1164.all;

ENTITY Ex2c_VHDL IS
  PORT (
  ------------------------------------------------------------------------------
  --Insert input ports below
    A        : IN  std_logic;                    -- input bit example
    B        : IN  std_logic;                    -- input bit example
    C        : IN  std_logic;                    -- input bit example
    D        : IN  std_logic;                    -- input bit example
  ------------------------------------------------------------------------------
  --Insert output ports below
    Z        : OUT std_logic                    -- output bit example
    );
END Ex2c_VHDL;

--------------------------------------------------------------------------------
--Complete your VHDL description below
--------------------------------------------------------------------------------

ARCHITECTURE TypeArchitecture OF Ex2c_VHDL IS

    signal u : std_logic; 
    signal v : std_logic; 
    signal t : std_logic;

BEGIN

    u <= (not A) and (not B) and (not C);
    v <= A and (not B) and (not C);
    t <= (not A) and (not B) and D;
    Z <= u or v or t;
    
END TypeArchitecture;
