// Logisim project ex2_a.circ as structural Verilog
module main (
  input  A,
  input  B,
  input  C,
  input  D,
  output X,
  output X_VHDL
);

  wire and_1_out, nor_1_out;

  nor nor_1 (nor_1_out, A, B);
  and and_1 (and_1_out, C, D);
  and and_2 (X, nor_1_out, and_1_out);
  Ex2a_VHDL ex2a_vhdl_1 (.A(A), .B(B), .C(C), .D(D), .X(X_VHDL));
endmodule

// VHDL entity Ex2a_VHDL, as the project stores it:
--------------------------------------------------------------------------------
-- Project :
-- File    :
-- Autor   :
-- Date    :
--
--------------------------------------------------------------------------------
-- Description :
--
--------------------------------------------------------------------------------

LIBRARY ieee;
USE ieee.std_logic_1164.all;

ENTITY Ex2a_VHDL IS
  PORT (
  ------------------------------------------------------------------------------
  --Insert input ports below
    A        : IN  std_logic;                    -- input bit example
    B        : IN  std_logic;                    -- input vector example
    C        : IN  std_logic;                    -- input vector example
    D        : IN  std_logic;                    -- input vector example
  ------------------------------------------------------------------------------
  --Insert output ports below
    X        : OUT std_logic                    -- output bit example
    );
END Ex2a_VHDL;

--------------------------------------------------------------------------------
--Complete your VHDL description below
--------------------------------------------------------------------------------

ARCHITECTURE TypeArchitecture OF Ex2a_VHDL IS

BEGIN

    X <= (not (A or B)) and (C and D);
   
END TypeArchitecture;
