// Logisim project ex2_b.circ as structural Verilog
module main (
  input  A,
  input  B,
  input  C,
  output Y,
  output Y_VHDL
);

  wire nor_1_out, not_1_out, not_2_out, not_3_out;

  not not_1 (not_1_out, A);
  not not_2 (not_2_out, B);
  nor nor_1 (nor_1_out, not_1_out, not_2_out);
  not not_3 (not_3_out, nor_1_out);
  Ex2b_VHDL ex2b_vhdl_1 (.A(A), .B(B), .C(C), .Y(Y_VHDL));
  and and_1 (Y, not_3_out, B, C);
endmodule

// VHDL entity Ex2b_VHDL, as the project stores it:
--------------------------------------------------------------------------------
-- Project :
-- File    :
-- Autor   :
-- Date    :
--
--------------------------------------------------------------------------------
-- Description :
--
--------------------------------------------------------------------------------

LIBRARY ieee;
USE ieee.std_logic_1164.all;

ENTITY Ex2b_VHDL IS
  PORT (
  ------------------------------------------------------------------------------
  --Insert input ports below
    A         : IN  std_logic;                    -- input bit example
    B         : IN  std_logic;                    -- input bit example
    C         : IN  std_logic;                    -- input bit example
  ------------------------------------------------------------------------------
  --Insert output ports below
    Y         : OUT std_logic                      -- output bit example
    );
END Ex2b_VHDL;

--------------------------------------------------------------------------------
--Complete your VHDL description below
--------------------------------------------------------------------------------

ARCHITECTURE TypeArchitecture OF Ex2b_VHDL IS

BEGIN

    Y <= (not (A and B)) and (B and C);

END TypeArchitecture;
