// Logisim project ex_01.circ as structural Verilog
module main (
  input  [3:0] KLM
);

  wire [6:0] dec_7s_1_c_7s, dec_7s_muxes_1_out_2;

  _7_Segment_Display u_7_segment_display_1 (
    .g(dec_7s_muxes_1_out_2[0]), .f(dec_7s_muxes_1_out_2[1]), .a(dec_7s_muxes_1_out_2[6]),
    .b(dec_7s_muxes_1_out_2[5]), .e(dec_7s_muxes_1_out_2[2]), .d(dec_7s_muxes_1_out_2[3]),
    .c(dec_7s_muxes_1_out_2[4]));  // open: dp
  dec_7s_muxes dec_7s_muxes_1 (.KLM(KLM), .out_2(dec_7s_muxes_1_out_2));
  _7_Segment_Display u_7_segment_display_2 (
    .g(dec_7s_1_c_7s[0]), .f(dec_7s_1_c_7s[1]), .a(dec_7s_1_c_7s[6]), .b(dec_7s_1_c_7s[5]),
    .e(dec_7s_1_c_7s[2]), .d(dec_7s_1_c_7s[3]), .c(dec_7s_1_c_7s[4]));  // open: dp
  dec_7s dec_7s_1 (.cnt_i(KLM), .c_7s(dec_7s_1_c_7s));

  // Other names for the same wires on the sheet: KLM_tunel[3:0] = KLM
endmodule

module dec_7s_muxes (
  input  [3:0] KLM,
  output [6:0] out_2
);

  Multiplexer #(.select(4)) multiplexer_1 (
    .in0(1'b1), .in1(1'b0), .in2(1'b1), .in3(1'b1), .in4(1'b0), .in5(1'b1), .in6(1'b1), .in7(1'b1),
    .in8(1'b1), .in9(1'b1), .in10(1'b1), .in11(1'b0), .in12(1'b1), .in13(1'b0), .in14(1'b0), .in15(1'b0),
    .out(out_2[6]), .sel(KLM));
  Multiplexer #(.select(4)) multiplexer_2 (
    .in0(1'b1), .in1(1'b1), .in2(1'b1), .in3(1'b1), .in4(1'b1), .in5(1'b0), .in6(1'b0), .in7(1'b1),
    .in8(1'b1), .in9(1'b1), .in10(1'b1), .in11(1'b0), .in12(1'b0), .in13(1'b1), .in14(1'b1), .in15(1'b1),
    .out(out_2[5]), .sel(KLM));
  Multiplexer #(.select(4)) multiplexer_3 (
    .in0(1'b1), .in1(1'b1), .in2(1'b0), .in3(1'b1), .in4(1'b1), .in5(1'b1), .in6(1'b1), .in7(1'b1),
    .in8(1'b1), .in9(1'b1), .in10(1'b1), .in11(1'b1), .in12(1'b0), .in13(1'b1), .in14(1'b1), .in15(1'b1),
    .out(out_2[4]), .sel(KLM));
  Multiplexer #(.select(4)) multiplexer_4 (
    .in0(1'b1), .in1(1'b0), .in2(1'b1), .in3(1'b1), .in4(1'b0), .in5(1'b1), .in6(1'b1), .in7(1'b0),
    .in8(1'b1), .in9(1'b1), .in10(1'b0), .in11(1'b1), .in12(1'b1), .in13(1'b1), .in14(1'b0), .in15(1'b1),
    .out(out_2[3]), .sel(KLM));
  Multiplexer #(.select(4)) multiplexer_5 (
    .in0(1'b1), .in1(1'b0), .in2(1'b1), .in3(1'b0), .in4(1'b0), .in5(1'b0), .in6(1'b1), .in7(1'b0),
    .in8(1'b1), .in9(1'b0), .in10(1'b1), .in11(1'b1), .in12(1'b1), .in13(1'b1), .in14(1'b0), .in15(1'b1),
    .out(out_2[2]), .sel(KLM));
  Multiplexer #(.select(4)) multiplexer_6 (
    .in0(1'b1), .in1(1'b0), .in2(1'b0), .in3(1'b0), .in4(1'b1), .in5(1'b1), .in6(1'b1), .in7(1'b0),
    .in8(1'b1), .in9(1'b1), .in10(1'b1), .in11(1'b1), .in12(1'b1), .in13(1'b0), .in14(1'b0), .in15(1'b0),
    .out(out_2[1]), .sel(KLM));
  Multiplexer #(.select(4)) multiplexer_7 (
    .in0(1'b0), .in1(1'b0), .in2(1'b1), .in3(1'b1), .in4(1'b1), .in5(1'b1), .in6(1'b1), .in7(1'b0),
    .in8(1'b1), .in9(1'b1), .in10(1'b1), .in11(1'b1), .in12(1'b0), .in13(1'b1), .in14(1'b0), .in15(1'b0),
    .out(out_2[0]), .sel(KLM));

  // Other names for the same wires on the sheet: N = KLM[0]; M = KLM[1]; L = KLM[2]; K = KLM[3]; G = out_2[0];
  //   F = out_2[1]; E = out_2[2]; D = out_2[3]; C = out_2[4]; B = out_2[5]; A = out_2[6]
endmodule

// VHDL entity dec_7s, as the project stores it:
library ieee;
use ieee.std_logic_1164.all;

-- Decodificador BCD para Display de 7 Segmentos
-- Pratica 3 - Circuitos Digitais
-- RA: 2719851 (impar)
-- Entrada: cnt_i(3 downto 0) = K L M N
-- Saida:   c_7s(6 downto 0)  = a b c d e f g
-- Display catodo comum (ativo em nivel alto)
-- 0x0 a 0xD: digitos hexadecimais 0 a D
-- 0xE: mostra ultimo digito do RA = 1
-- 0xF: RA impar -> mostra letra J

entity dec_7s is
    port(
        --Entradas (4 bits)
        cnt_i : in  std_logic_vector(3 downto 0);
        --Saidas (7 bits)
        c_7s  : out std_logic_vector(6 downto 0)
    );
end dec_7s;

architecture decode of dec_7s is
begin
    --              abcdefg          klmn
    with cnt_i select
        c_7s <= "1111110" when "0000",  -- 0  -> 7E h
                "0110000" when "0001",  -- 1  -> 30 h
                "1101101" when "0010",  -- 2  -> 6D h
                "1111001" when "0011",  -- 3  -> 79 h
                "0110011" when "0100",  -- 4  -> 33 h
                "1011011" when "0101",  -- 5  -> 5B h
                "1011111" when "0110",  -- 6  -> 5F h
                "1110000" when "0111",  -- 7  -> 70 h
                "1111111" when "1000",  -- 8  -> 7F h
                "1111011" when "1001",  -- 9  -> 7B h
                "1110111" when "1010",  -- A  -> 77 h
                "0011111" when "1011",  -- b  -> 1F h
                "1001110" when "1100",  -- C  -> 4E h
                "0111101" when "1101",  -- d  -> 3D h
                "0110000" when "1110",  -- E  -> mostra '1' (ultimo digito RA 2719851)
                "0111100" when "1111",  -- F  -> mostra 'J' (RA impar)
                "0000000" when others;
end decode;
