// Logisim project ex1.circ as structural Verilog
module main (
  output Q_latch_nand,
  output QN_latch_nor,
  output QN_latch_nand,
  output Q_latch_nor,
  output Q_latch_nand_VHDL,
  output Q_latch_nor_VHDL,
  output QN_latch_nand_VHDL,
  output QN_latch_nor_VHDL
);

  wire R_nand, R_nor, S_nand, S_nor;

  Button #(.press("passive")) SET_nand (.out(S_nand));
  Button #(.press("passive")) RESET_nand (.out(R_nand));
  nand nand_1 (Q_latch_nand, S_nand, QN_latch_nand);
  nand nand_2 (QN_latch_nand, Q_latch_nand, R_nand);
  latch_sr_nand latch_sr_nand_1 (.S(S_nand), .R(R_nand), .Q(Q_latch_nand_VHDL), .QN(QN_latch_nand_VHDL));
  Button SET_nor (.out(S_nor));
  Button RESET_nor (.out(R_nor));
  nor nor_1 (QN_latch_nor, S_nor, Q_latch_nor);
  nor nor_2 (Q_latch_nor, QN_latch_nor, R_nor);
  latch_sr_nor latch_sr_nor_1 (.S(S_nor), .R(R_nor), .Q(Q_latch_nor_VHDL), .QN(QN_latch_nor_VHDL));
endmodule

// VHDL entity latch_sr_nand, as the project stores it:
library ieee;
use ieee.std_logic_1164.all;

entity latch_sr_nand is
  port(
    S, R  : in  std_logic;      -- SET e RESET
    Q, QN : out std_logic       -- Saídas Q e Q invertido
  );
end latch_sr_nand;

architecture type_architecture of latch_sr_nand is
  signal qstate: std_logic;
begin

  -- Bloco de processo
  process(S, R) -- Lista de sensitividade
  begin
    if S = '0' and R = '1' then 
        qstate <= '1';
    elsif S = '1' and R = '0' then 
        qstate <= '0';
    end if;
  end process;

  Q  <= qstate;
  QN <= not qstate;

end type_architecture;

// VHDL entity latch_sr_nor, as the project stores it:
-- Exercicio 1b) Latch SR com portas NOR
-- Entradas ativas em alto (S, R)
-- Tabela verdade:
--    S   R  |  Q   QN
--    0   0  |  Q   QN  (memoria)
--    0   1  |  0   1   (reset)
--    1   0  |  1   0   (set)
--    1   1  |  0   0   (proibido)

library ieee;
use ieee.std_logic_1164.all;

entity latch_sr_nor is
  port(
    S, R  : in  std_logic;
    Q, QN : out std_logic
  );
end latch_sr_nor;

architecture latch_sr_nor_arch of latch_sr_nor is
  signal q_i, qn_i : std_logic;
begin
  q_i  <= R nor qn_i;
  qn_i <= S nor q_i;
  Q    <= q_i;
  QN   <= qn_i;
end latch_sr_nor_arch;
