// Logisim project ex2.circ as structural Verilog
module main (
  input  in_1,
  input  in_2,
  input  in_3,
  input  in_4,
  input  in_5,
  input  in_6,
  input  in_7,
  input  in_8,
  output Q,
  output Q_nor,
  output QN,
  output QN_nor,
  output Q_nor_VHDL,
  output Q_nand_VHDL,
  output QN_nor_VHDL,
  output QN_nand_VHDL,
  output Q_otim,
  output Q_nor_otim,
  output QN_otim,
  output QN_nor_otim,
  output Q_nand_VHDL_otim,
  output Q_nor_VHDL_otim,
  output QN_nand_VHDL_otim,
  output QN_nor_VHDL_otim
);

  wire nand_1_out, nand_2_out, nand_3_out, nand_4_out, nor_1_out, nor_2_out, nor_3_out, nor_6_out, not_1_out,
       not_2_out, not_3_out;

  Button D_nand ();  // open: out
  Button ENABLE_nand ();  // open: out
  not not_1 (not_1_out, in_2);
  latch_d_nand latch_d_nand_1 (.D(in_2), .EN(in_3), .Q(Q_nand_VHDL), .QN(QN_nand_VHDL));
  nand nand_1 (nand_1_out, in_5, in_7);
  latch_d_nand latch_d_nand_2 (.D(in_5), .EN(in_7), .Q(Q_nand_VHDL_otim), .QN(QN_nand_VHDL_otim));
  nand nand_2 (nand_2_out, in_2, in_3);
  nand nand_3 (nand_3_out, in_3, not_1_out);
  nand nand_4 (nand_4_out, nand_1_out, in_7);
  nand nand_5 (Q, nand_2_out, QN);
  nand nand_6 (QN, Q, nand_3_out);
  nand nand_7 (Q_otim, nand_1_out, QN_otim);
  nand nand_8 (QN_otim, Q_otim, nand_4_out);
  Button D_nor ();  // open: out
  Button ENABLE_nor ();  // open: out
  not not_2 (not_2_out, in_4);
  not not_3 (not_3_out, in_1);
  nor nor_1 (nor_1_out, in_1, not_2_out);
  nor nor_2 (nor_2_out, not_2_out, not_3_out);
  latch_d_nor latch_d_nor_1 (.D(in_1), .EN(in_4), .Q(Q_nor_VHDL), .QN(QN_nor_VHDL));
  latch_d_nand latch_d_nand_3 (.D(in_6), .EN(in_8), .Q(Q_nor_VHDL_otim), .QN(QN_nor_VHDL_otim));
  nor nor_3 (nor_3_out, in_6, in_8);
  nor nor_4 (Q_nor, nor_1_out, QN_nor);
  nor nor_5 (QN_nor, Q_nor, nor_2_out);
  nor nor_6 (nor_6_out, nor_3_out, in_8);
  nor nor_7 (Q_nor_otim, nor_3_out, QN_nor_otim);
  nor nor_8 (QN_nor_otim, Q_nor_otim, nor_6_out);

  // Other names for the same wires on the sheet: D_nand = in_2; D_nand_otim = in_5; D_nor = in_1; D_nor_otim = in_6;
  //   ENABLE_nand = in_3; ENABLE_nand_otim = in_7; ENABLE_nor = in_4; ENABLE_nor_otim = in_8

  // Notes on the sheet:
  //   Otimizado para 4 portas NAND:
  //   Otimizado para 4 portas NOR:
endmodule

// VHDL entity latch_d_nand, as the project stores it:
-- Exercicio 2a) Latch D transparente com portas NAND (versao otimizada 4 NANDs)
-- Quando EN=1, Q segue D; quando EN=0, mantem estado.
-- Tabela verdade:
--   EN  D  |  Q     QN
--    0  x  |  Q     QN   (memoria)
--    1  0  |  0     1
--    1  1  |  1     0

library ieee;
use ieee.std_logic_1164.all;

entity latch_d_nand is
  port(
    D, EN : in  std_logic;	-- entradas: habilitação e dados
    Q, QN : out std_logic	-- saídas: Q e Q invertido
  );
end latch_d_nand;

architecture latch_d_nand_arch of latch_d_nand is
  signal qstate: std_logic;	-- sinal interno para guardar o estado
  
begin
  -- processo sensível a EN e D
  process(EN, D) 
  begin
    if EN = '1' then qstate <= D;            -- transparência habilitada
    end if;                                  -- ausência de "else" mantém estado anterior
  end process;

  Q  <= qstate;
  QN <= not qstate;
  
end latch_d_nand_arch;

// VHDL entity latch_d_nor, as the project stores it:
-- Exercicio 2b) Latch D transparente com portas NOR (versao otimizada 4 NORs)
-- Quando EN=1, Q segue D; quando EN=0, mantem estado.

library ieee;
use ieee.std_logic_1164.all;

entity latch_d_nor is
  port(
    D, EN : in  std_logic;      -- entradas: habilitação e dados
    Q, QN : out std_logic       -- saídas: Q e Q invertido
  );
end latch_d_nor;

architecture arch_latch of latch_d_nor is
  signal qstate: std_logic;     -- sinal interno de memória
  
begin

  process(EN, D) 
  begin
    if EN = '1' then qstate <= D;            -- estado transparente: Q copia D
    end if;                                  -- inferência de memória quando EN = '0'
  end process;

  Q  <= qstate;
  QN <= not qstate;

end arch_latch;
