// Logisim project ex3_a.circ as structural Verilog
module main (
  input  D,
  input  CLK,
  output Q,
  output QN,
  output out_5,
  output out_6,
  output Q_VHDL,
  output QN_VHDL,
  output Q_otim,
  output QN_otim,
  output Q_VHDL_otim,
  output QN_VHDL_otim
);

  wire d_ff_1_q, nand1_out, nand2_out, nand_1_out, nand_2_out, nand_3_out, nand_4_out, nand_5_out,
       nand_6_out, nor1_out, nor2_out, nor3_out, nor4_out, not_1_out, not_2_out;

  not not_1 (not_1_out, CLK);
  not not_2 (not_2_out, CLK);
  nand nand_1 (nand_1_out, D, not_1_out);
  nor nor1 (nor1_out, D, CLK);
  D_Flip_Flop #(.trigger("high")) d_ff_1 (.D(D), .clk(not_2_out), .Q(d_ff_1_q));  // open: Qn, preset, reset
  nor nor2 (nor2_out, nor1_out, CLK);
  nand nand_2 (nand_2_out, nand_1_out, not_1_out);
  D_Flip_Flop #(.trigger("high")) d_ff_2 (.D(d_ff_1_q), .clk(CLK), .Q(Q), .Qn(QN));  // open: preset, reset
  nand nand_3 (nand_3_out, nand_1_out, nand_4_out);
  nand nand_4 (nand_4_out, nand_3_out, nand_2_out);
  nor nor3 (nor3_out, nor1_out, nor4_out);
  nor nor4 (nor4_out, nor3_out, nor2_out);
  ff_d_me_pos ff_d_me_pos_1 (.D(D), .CLK(CLK), .Q(Q_VHDL_otim), .QN(QN_VHDL_otim));
  ff_d_me_pos ff_d_me_pos_2 (.D(D), .CLK(CLK), .Q(Q_VHDL), .QN(QN_VHDL));
  nand nand_5 (nand_5_out, nand_3_out, CLK);
  nand nand1 (nand1_out, nor3_out, CLK);
  nand nand_6 (nand_6_out, nand_5_out, CLK);
  nand nand2 (nand2_out, nand1_out, CLK);
  nand nand_7 (out_5, nand_5_out, out_6);
  nand nand_8 (out_6, out_5, nand_6_out);
  nand nand3 (Q_otim, nand1_out, QN_otim);
  nand nand4 (QN_otim, Q_otim, nand2_out);

  // Notes on the sheet:
  //   3.a1)
  //   3.a2)
  //   Latch D Nand
  //   Mestre
  //   Latch D Nand
  //   Escravo
endmodule

// VHDL entity ff_d_me_pos, as the project stores it:
-- Exercicio 3a) Flip-flop D mestre-escravo com resposta a borda POSITIVA do clock
-- Estrutura: dois latches D em cascata
--   - Latch mestre transparente quando CLK=0 (usa CLK invertido como EN)
--   - Latch escravo transparente quando CLK=1
-- Efeito liquido: Q copia D na subida do clock.
-- Tabela verdade:
--   CLK (borda)  D  |  Q(t+)
--       ^          0 |   0
--       ^          1 |   1
--       outro      x |   Q (mantem)

library ieee;
use ieee.std_logic_1164.all;

-----------------------------------------------
entity ff_d_me_pos is
  port(
    D, CLK : in  std_logic;
    Q, QN  : out std_logic
  );
end ff_d_me_pos;
-----------------------------------------------

architecture latches of ff_d_me_pos is

  signal s1 : std_logic;      -- nó interligando latches
  signal qs : std_logic;      -- nó para saída do escravo

begin

  latch1: process(CLK, D)      -- latch mestre: transparente em CLK='0'
  begin
    if CLK = '0' then s1 <= D;
    end if;
  end process latch1;

  latch2: process(CLK, s1)     -- latch escravo: transparente em CLK='1'
  begin
    if CLK = '1' then qs <= s1;
    end if;
  end process latch2;

  Q  <= qs;
  QN <= not qs;
  
end latches;

// VHDL entity ff_d_me_neg, as the project stores it:
-- Exercicio 3b) Flip-flop D mestre-escravo com resposta a borda NEGATIVA do clock
-- Estrutura inversa da versao positiva: mestre transparente em CLK=1,
-- escravo transparente em CLK=0; efeito: copia D na descida.

library ieee;
use ieee.std_logic_1164.all;

entity ff_d_me_neg is
  port(
    D, CLK : in  std_logic;
    Q, QN  : out std_logic
  );
end ff_d_me_neg;

architecture ff_d_me_neg_arch of ff_d_me_neg is
  signal qm, qs : std_logic := '0';
begin
  process(CLK, D)
  begin
    if CLK = '1' then
      qm <= D;
    end if;
    if CLK = '0' then
      qs <= qm;
    end if;
  end process;
  Q  <= qs;
  QN <= not qs;
end ff_d_me_neg_arch;
