// Logisim project ex3_b.circ as structural Verilog
module main (
  input  D,
  input  CLK,
  output out_3,
  output out_4,
  output Q_VHDL,
  output QN_VHDL,
  output Q_otim,
  output QN_otim,
  output Q_VHDL_otim,
  output QN_VHDL_otim
);

  wire nand_1_out, nand_2_out, nand_3_out, nand_4_out, nor_1_out, nor_2_out, nor_3_out, nor_4_out, nor_5_out,
       nor_6_out, nor_7_out, nor_8_out, not_1_out;

  not not_1 (not_1_out, CLK);
  nand nand_1 (nand_1_out, D, CLK);
  nor nor_1 (nor_1_out, D, not_1_out);
  nand nand_2 (nand_2_out, nand_1_out, CLK);
  nor nor_2 (nor_2_out, nor_1_out, not_1_out);
  ff_d_me_neg ff_d_me_neg_1 (.D(D), .CLK(CLK), .Q(Q_VHDL), .QN(QN_VHDL));
  nand nand_3 (nand_3_out, nand_1_out, nand_4_out);
  nand nand_4 (nand_4_out, nand_3_out, nand_2_out);
  ff_d_me_neg ff_d_me_neg_2 (.D(D), .CLK(CLK), .Q(Q_VHDL_otim), .QN(QN_VHDL_otim));
  nor nor_3 (nor_3_out, nor_1_out, nor_4_out);
  nor nor_4 (nor_4_out, nor_3_out, nor_2_out);
  nor nor_5 (nor_5_out, nor_3_out, CLK);
  nor nor_6 (nor_6_out, nand_3_out, CLK);
  nor nor_7 (nor_7_out, nor_5_out, CLK);
  nor nor_8 (nor_8_out, nor_6_out, CLK);
  nor nor_9 (out_3, nor_5_out, out_4);
  nor nor_10 (out_4, out_3, nor_7_out);
  nor nor_11 (Q_otim, nor_6_out, QN_otim);
  nor nor_12 (QN_otim, Q_otim, nor_8_out);

  // Notes on the sheet:
  //   3.b1)
  //   3.b2)
endmodule

// VHDL entity ff_d_me_neg, as the project stores it:
-- Exercicio 3b) Flip-flop D mestre-escravo com resposta a borda NEGATIVA do clock
-- Estrutura inversa da versao positiva: mestre transparente em CLK=1,
-- escravo transparente em CLK=0; efeito: copia D na descida.

library ieee;
use ieee.std_logic_1164.all;

entity ff_d_me_neg is
  port(
    D, CLK : in  std_logic;
    Q, QN  : out std_logic
  );
end ff_d_me_neg;

architecture latches of ff_d_me_neg is

  signal s1 : std_logic;    -- nó interligando latches
  signal qs : std_logic;    -- nó para saída do escravo
  
begin

  latch1: process(CLK, D)        -- Mestre: transparente em CLK='1'
  begin
    if CLK = '1' then s1 <= D;
    end if;
  end process latch1;

  latch2: process(CLK, s1)       -- Escravo: transparente em CLK='0'
  begin
    if CLK = '0' then qs <= s1;
    end if;
  end process latch2;

  Q  <= qs;
  QN <= not qs;
  
end latches;
