// Logisim project ex4.circ as structural Verilog
module main (
  input  J,
  input  K,
  input  CLRN,
  input  PRN,
  input  CLK,
  input  T,
  output Q_b,
  output QN_b,
  output Q_VHDL_ff_jk_descritiva,
  output QN_VHDL_ff_jk_descritiva,
  output Q_VHDL_ff_jk_logica,
  output QN_VHDL_ff_jk_logica,
  output Q_c,
  output QN_c,
  output Q_VHDL_ff_t_descritiva,
  output QN_VHDL_ff_t_descritiva,
  output Q_VHDL_ff_t_logica,
  output QN_VHDL_ff_t_logica
);

  wire and_1_out, and_2_out, not_1_out, or_1_out, xor_1_out;

  ex4a_ff_d ex4a_ff_d_1 (.D(or_1_out), .CLRN(CLRN), .PRN(PRN), .CLK(CLK), .Q(Q_b), .QN(QN_b));
  not not_1 (not_1_out, K);
  ff_jk_descritiva ff_jk_descritiva_1 (
    .J(J), .K(K), .CLRN(CLRN), .PRN(PRN), .CLK(CLK), .Q(Q_VHDL_ff_jk_descritiva),
    .QN(QN_VHDL_ff_jk_descritiva));
  ff_jk_logica ff_jk_logica_1 (
    .J(J), .K(K), .CLRN(CLRN), .PRN(PRN), .CLK(CLK), .Q(Q_VHDL_ff_jk_logica), .QN(QN_VHDL_ff_jk_logica));
  ex4a_ff_d ex4a_ff_d_2 (.D(xor_1_out), .CLRN(CLRN), .PRN(PRN), .CLK(CLK), .Q(Q_c), .QN(QN_c));
  ff_t_descritiva ff_t_descritiva_1 (
    .T(T), .CLRN(CLRN), .PRN(PRN), .CLK(CLK), .Q(Q_VHDL_ff_t_descritiva), .QN(QN_VHDL_ff_t_descritiva));
  ff_t_logica ff_t_logica_1 (
    .T(T), .CLRN(CLRN), .PRN(PRN), .CLK(CLK), .Q(Q_VHDL_ff_t_logica), .QN(QN_VHDL_ff_t_logica));
  and and_1 (and_1_out, J, QN_b);
  and and_2 (and_2_out, Q_b, not_1_out);
  xor xor_1 (xor_1_out, T, Q_c);
  or or_1 (or_1_out, and_1_out, and_2_out);

  // Notes on the sheet:
  //   4.b)
  //   4.c)
endmodule

// VHDL entity ff_jk_logica, as the project stores it:
-- Exercicio 4b) Flip-flop JK emulado a partir de FF D - VERSAO EXPRESSAO LOGICA
-- D = J.Q' + K'.Q   (obtido pelo mapa de Karnaugh da conversao JK -> D)

library ieee;
use ieee.std_logic_1164.all;

entity ff_jk_logica is
  port(
    J, K, CLRN, PRN, CLK : in  std_logic;
    Q, QN                : out std_logic
  );
end ff_jk_logica;

architecture behavior of ff_jk_logica is

  signal qstate : std_logic;
  
begin
  process(CLK, PRN, CLRN)
  begin
    if    CLRN = '0' then qstate <= '0';
    elsif PRN  = '0' then qstate <= '1';
    elsif CLK = '1' and CLK'event then      -- Ajustado para borda positiva 
	  -- Aplicação da expressão booleana
      qstate <= (J and (not qstate)) or ((not K) and qstate);
    end if;
  end process;
  
  Q  <= qstate;
  QN <= not qstate;
  
end behavior;

// VHDL entity ff_jk_descritiva, as the project stores it:
-- Exercicio 4b) Flip-flop JK emulado a partir de FF D - VERSAO DESCRITIVA
-- Resposta a borda POSITIVA do clock, PRN/CLRN assincronos ativos em baixo.
-- Tabela verdade:
--   J K | Q(t+)
--   0 0 |  Q
--   0 1 |  0
--   1 0 |  1
--   1 1 |  not Q

library ieee;
use ieee.std_logic_1164.all;

entity ff_jk_descritiva is
  port(
    J, K, CLRN, PRN, CLK : in  std_logic;
    Q, QN                : out std_logic
  );
end ff_jk_descritiva;

architecture behavior of ff_jk_descritiva is

  signal qstate : std_logic;
  
begin

  process(CLK, PRN, CLRN)
  begin
    if    CLRN = '0' then qstate <= '0';
    elsif PRN  = '0' then qstate <= '1';
    
	elsif CLK = '1' and CLK'event then       -- Ajustado para borda positiva
      if    J = '1' and K = '1' then qstate <= not qstate;    -- Toggle
      elsif J = '1' and K = '0' then qstate <= '1';           -- Set
      elsif J = '0' and K = '1' then qstate <= '0';           -- Reset
      end if;
    end if;
  end process;
  
  Q  <= qstate;
  QN <= not qstate;
  
end behavior;

// VHDL entity ex4a_ff_d, as the project stores it:
-- Exercicio 4a) Flip-flop D com resposta a borda POSITIVA do clock
-- Entradas preset (PRN) e clear (CLRN) assincronas, ativas em baixo.
-- Tabela verdade:
--   CLRN PRN CLK D | Q
--    0    x   x  x | 0
--    1    0   x  x | 1
--    1    1   ^  D | D
--    1    1 outro x| Q (mantem)

library ieee;
use ieee.std_logic_1164.all;

entity ex4a_ff_d is
  port(
    D, CLRN, PRN, CLK : in  std_logic;
    Q, QN             : out std_logic
  );
end ex4a_ff_d;

architecture behavior of ex4a_ff_d is

  signal qstate : std_logic;

begin

  process(CLK, PRN, CLRN)
  begin
    if    CLRN = '0' then qstate <= '0';           -- O Clear tem a maior prioridade e força 0 na saída
    elsif PRN  = '0' then qstate <= '1';           -- O Present tem a segunda maior prioridade e força 1 na saída
	
	-- Se nem Clear nem Preset estão ativos (ambos em '1'),
	-- o circuito opera normalment na borda de subida do clock
    elsif CLK = '1' and CLK'event then qstate <= D;  
    end if;
  end process;
  
  Q  <= qstate;
  QN <= not qstate;

end behavior;

// VHDL entity ff_t_logica, as the project stores it:
-- Exercicio 4c) Flip-flop T emulado a partir de FF D - VERSAO EXPRESSAO LOGICA
-- D = T xor Q

library ieee;
use ieee.std_logic_1164.all;

entity ff_t_logica is
  port(
    T, CLRN, PRN, CLK : in  std_logic;
    Q, QN             : out std_logic
  );
end ff_t_logica;

architecture behavior of ff_t_logica is

  signal qstate : std_logic;
  
begin
  process(CLK, PRN, CLRN)
  begin
    if    CLRN = '0' then qstate <= '0';
    elsif PRN  = '0' then qstate <= '1';
    elsif CLK = '1' and CLK'event then     -- Borda POSITIVA
	  -- Expressão booleana D = T XOR Q
      qstate <= T xor qstate;
    end if;
  end process;
  
  Q  <= qstate;
  QN <= not qstate;
  
end behavior;

// VHDL entity ff_t_descritiva, as the project stores it:
-- Exercicio 4c) Flip-flop T emulado a partir de FF D - VERSAO DESCRITIVA
-- Resposta a borda POSITIVA, PRN/CLRN assincronos ativos em baixo.
-- Tabela: T=0 -> Q mantem; T=1 -> Q = not Q (toggle).

library ieee;
use ieee.std_logic_1164.all;

entity ff_t_descritiva is
  port(
    T, CLRN, PRN, CLK : in  std_logic;
    Q, QN             : out std_logic
  );
end ff_t_descritiva;

architecture behavior of ff_t_descritiva is

  signal qstate : std_logic;
  
begin
  process(CLK, PRN, CLRN)
  begin
    if    CLRN = '0' then qstate <= '0';
    elsif PRN  = '0' then qstate <= '1';
    elsif CLK = '1' and CLK'event then         -- borda POSITIVA
      if T = '1' then qstate <= not qstate;    -- Toogle
      end if;
    end if;
  end process;
  
  Q  <= qstate;
  QN <= not qstate;
  
end behavior;
