// Logisim project pratica4.circ as structural Verilog
module main (
);


  // Notes on the sheet:
  //   Pratica 4 - Circuitos Digitais (Prof. Gortan)
  //   Abra cada VHDL Entity na arvore do projeto (painel a esquerda)
  //   e arraste-o para este circuito 'main' para testar.
  //   Ex.1: latch_sr_nand, latch_sr_nor
  //   Ex.2: latch_d_nand, latch_d_nor
  //   Ex.3: ff_d_me_pos, ff_d_me_neg
  //   Ex.4: ff_d, ff_jk_descritiva, ff_jk_logica, ff_t_descritiva, ff_t_logica
endmodule

// VHDL entity latch_sr_nand, as the project stores it:
library ieee;
use ieee.std_logic_1164.all;

entity latch_sr_nand is
  port(
    S_n, R_n : in  std_logic;
    Q, QN    : out std_logic
  );
end latch_sr_nand;

architecture latch_sr_nand_arch of latch_sr_nand is
  signal q_i, qn_i : std_logic;
begin
  q_i  <= S_n nand qn_i;
  qn_i <= R_n nand q_i;
  Q    <= q_i;
  QN   <= qn_i;
end latch_sr_nand_arch;

// VHDL entity latch_sr_nor, as the project stores it:
library ieee;
use ieee.std_logic_1164.all;

entity latch_sr_nor is
  port(
    S, R  : in  std_logic;
    Q, QN : out std_logic
  );
end latch_sr_nor;

architecture latch_sr_nor_arch of latch_sr_nor is
  signal q_i, qn_i : std_logic;
begin
  q_i  <= R nor qn_i;
  qn_i <= S nor q_i;
  Q    <= q_i;
  QN   <= qn_i;
end latch_sr_nor_arch;

// VHDL entity latch_d_nand, as the project stores it:
library ieee;
use ieee.std_logic_1164.all;

entity latch_d_nand is
  port(
    D, EN : in  std_logic;
    Q, QN : out std_logic
  );
end latch_d_nand;

architecture latch_d_nand_arch of latch_d_nand is
  signal s_n, r_n : std_logic;
  signal q_i, qn_i : std_logic;
begin
  s_n <= D nand EN;
  r_n <= (not D) nand EN;
  q_i  <= s_n nand qn_i;
  qn_i <= r_n nand q_i;
  Q  <= q_i;
  QN <= qn_i;
end latch_d_nand_arch;

// VHDL entity latch_d_nor, as the project stores it:
library ieee;
use ieee.std_logic_1164.all;

entity latch_d_nor is
  port(
    D, EN : in  std_logic;
    Q, QN : out std_logic
  );
end latch_d_nor;

architecture latch_d_nor_arch of latch_d_nor is
  signal s_i, r_i : std_logic;
  signal q_i, qn_i : std_logic;
begin
  s_i <= not ((not D) nor (not EN));
  r_i <= not (D       nor (not EN));
  q_i  <= r_i nor qn_i;
  qn_i <= s_i nor q_i;
  Q  <= q_i;
  QN <= qn_i;
end latch_d_nor_arch;

// VHDL entity ff_d_me_pos, as the project stores it:
library ieee;
use ieee.std_logic_1164.all;

entity ff_d_me_pos is
  port(
    D, CLK : in  std_logic;
    Q, QN  : out std_logic
  );
end ff_d_me_pos;

architecture ff_d_me_pos_arch of ff_d_me_pos is
  signal qm, qs : std_logic := '0';
begin
  process(CLK, D)
  begin
    if CLK = '0' then
      qm <= D;
    end if;
    if CLK = '1' then
      qs <= qm;
    end if;
  end process;
  Q  <= qs;
  QN <= not qs;
end ff_d_me_pos_arch;

// VHDL entity ff_d_me_neg, as the project stores it:
library ieee;
use ieee.std_logic_1164.all;

entity ff_d_me_neg is
  port(
    D, CLK : in  std_logic;
    Q, QN  : out std_logic
  );
end ff_d_me_neg;

architecture ff_d_me_neg_arch of ff_d_me_neg is
  signal qm, qs : std_logic := '0';
begin
  process(CLK, D)
  begin
    if CLK = '1' then
      qm <= D;
    end if;
    if CLK = '0' then
      qs <= qm;
    end if;
  end process;
  Q  <= qs;
  QN <= not qs;
end ff_d_me_neg_arch;

// VHDL entity ff_d, as the project stores it:
library ieee;
use ieee.std_logic_1164.all;

entity ff_d is
  port(
    D, CLK, PRN, CLRN : in  std_logic;
    Q, QN             : out std_logic
  );
end ff_d;

architecture ff_d_arch of ff_d is
  signal qstate : std_logic;
begin
  process(CLK, PRN, CLRN)
  begin
    if    CLRN = '0' then qstate <= '0';
    elsif PRN  = '0' then qstate <= '1';
    elsif CLK = '1' and CLK'event then
      qstate <= D;
    end if;
  end process;
  Q  <= qstate;
  QN <= not qstate;
end ff_d_arch;

// VHDL entity ff_jk_descritiva, as the project stores it:
library ieee;
use ieee.std_logic_1164.all;

entity ff_jk_descritiva is
  port(
    J, K, CLK, PRN, CLRN : in  std_logic;
    Q, QN                : out std_logic
  );
end ff_jk_descritiva;

architecture ff_jk_descritiva_arch of ff_jk_descritiva is
  signal qstate : std_logic;
begin
  process(CLK, PRN, CLRN)
  begin
    if    CLRN = '0' then qstate <= '0';
    elsif PRN  = '0' then qstate <= '1';
    elsif CLK = '1' and CLK'event then
      if    J = '1' and K = '1' then qstate <= not qstate;
      elsif J = '1' and K = '0' then qstate <= '1';
      elsif J = '0' and K = '1' then qstate <= '0';
      end if;
    end if;
  end process;
  Q  <= qstate;
  QN <= not qstate;
end ff_jk_descritiva_arch;

// VHDL entity ff_jk_logica, as the project stores it:
library ieee;
use ieee.std_logic_1164.all;

entity ff_jk_logica is
  port(
    J, K, CLK, PRN, CLRN : in  std_logic;
    Q, QN                : out std_logic
  );
end ff_jk_logica;

architecture ff_jk_logica_arch of ff_jk_logica is
  signal qstate : std_logic;
begin
  process(CLK, PRN, CLRN)
  begin
    if    CLRN = '0' then qstate <= '0';
    elsif PRN  = '0' then qstate <= '1';
    elsif CLK = '1' and CLK'event then
      qstate <= (J and (not qstate)) or ((not K) and qstate);
    end if;
  end process;
  Q  <= qstate;
  QN <= not qstate;
end ff_jk_logica_arch;

// VHDL entity ff_t_descritiva, as the project stores it:
library ieee;
use ieee.std_logic_1164.all;

entity ff_t_descritiva is
  port(
    T, CLK, PRN, CLRN : in  std_logic;
    Q, QN             : out std_logic
  );
end ff_t_descritiva;

architecture ff_t_descritiva_arch of ff_t_descritiva is
  signal qstate : std_logic;
begin
  process(CLK, PRN, CLRN)
  begin
    if    CLRN = '0' then qstate <= '0';
    elsif PRN  = '0' then qstate <= '1';
    elsif CLK = '1' and CLK'event then
      if T = '1' then qstate <= not qstate;
      end if;
    end if;
  end process;
  Q  <= qstate;
  QN <= not qstate;
end ff_t_descritiva_arch;

// VHDL entity ff_t_logica, as the project stores it:
library ieee;
use ieee.std_logic_1164.all;

entity ff_t_logica is
  port(
    T, CLK, PRN, CLRN : in  std_logic;
    Q, QN             : out std_logic
  );
end ff_t_logica;

architecture ff_t_logica_arch of ff_t_logica is
  signal qstate : std_logic;
begin
  process(CLK, PRN, CLRN)
  begin
    if    CLRN = '0' then qstate <= '0';
    elsif PRN  = '0' then qstate <= '1';
    elsif CLK = '1' and CLK'event then
      qstate <= T xor qstate;
    end if;
  end process;
  Q  <= qstate;
  QN <= not qstate;
end ff_t_logica_arch;
