// Logisim project Lab_05_P1_info.circ as structural Verilog
module componentes (
);

  dff vhdl ();  // open: d, clk, prs, clr, q, qn

  // Notes on the sheet:
  //   Este era o circuito "main"
  //   Caso o componente não receba um rótulo,
  //   Foi renomeado para "componentes"
  //   para lembrar que armazena os componentes VHDL
  //   O componente "dff" recebeu o rótulo (label) "vhdl" (em azul)
  //   para que o o Logisim o renomeie para "dff_vhdl"
  //   o Logisim utilizará um rótulo padrão tipo "component_0",
  //   o que dificultará sua utilização em outros circuitos deste projeto
  //   Para que a utilização deste (e outros possíveis) componentes
  //   nos passos seguintes seja bem sucedida, é preciso  que o componente
  //   já tenha sido previamente compilado, ou não será reconhecido pelo Logisim
  //   Os demais circuitos deverão referenciar esse componente portanto como "dff_vhdl"
endmodule

module P1_cnt_up_mod16 (
);

  wire CLK_out, FF0_qn, FF1_qn, FF2_qn, FF3_qn, not_1_out, Q0, Q1, Q2, Q3, Z_out;
  wire [3:0] cnt_up_mod16_1_q;

  Clock CLK (.out(CLK_out));
  Button #(.press("passive")) Z (.out(Z_out));
  D_Flip_Flop FF0 (.D(FF0_qn), .clk(CLK_out), .Q(Q0), .Qn(FF0_qn), .reset(not_1_out));  // open: preset
  not not_1 (not_1_out, Z_out);
  D_Flip_Flop FF1 (.D(FF1_qn), .clk(FF0_qn), .Q(Q1), .Qn(FF1_qn), .reset(not_1_out));  // open: preset
  D_Flip_Flop FF2 (.D(FF2_qn), .clk(FF1_qn), .Q(Q2), .Qn(FF2_qn), .reset(not_1_out));  // open: preset
  Hex_Digit_Display hex_digit_display_1 (.value(cnt_up_mod16_1_q));  // open: dp
  cnt_up_mod16 cnt_up_mod16_1 (.clk(CLK_out), .z(Z_out), .q(cnt_up_mod16_1_q));
  D_Flip_Flop FF3 (.D(FF3_qn), .clk(FF2_qn), .Q(Q3), .Qn(FF3_qn), .reset(not_1_out));  // open: preset
  Hex_Digit_Display hex_digit_display_2 (.value({Q3, Q2, Q1, Q0}));  // open: dp

  // Notes on the sheet:
  //   Botão simula a tecla Z - ativo baixo
endmodule

module P2_cnt_up_mod10 (
);

  wire CLK_out, FF0_qn, FF1_qn, FF2_qn, FF3_qn, nand_1_out, nand_2_out, not_1_out, Q0, Q1, Q2, Q3, Z_out;
  wire [3:0] cnt_up_mod16_1_q;

  nand nand_1 (nand_1_out, nand_2_out, Z_out);
  Clock CLK (.out(CLK_out));
  Button #(.press("passive")) Z (.out(Z_out));
  D_Flip_Flop FF0 (.D(FF0_qn), .clk(CLK_out), .Q(Q0), .Qn(FF0_qn), .reset(not_1_out));  // open: preset
  not not_1 (not_1_out, Z_out);
  nand nand_2 (nand_2_out, Q3, Q1);
  D_Flip_Flop FF1 (.D(FF1_qn), .clk(FF0_qn), .Q(Q1), .Qn(FF1_qn), .reset(nand_1_out));  // open: preset
  D_Flip_Flop FF2 (.D(FF2_qn), .clk(FF1_qn), .Q(Q2), .Qn(FF2_qn), .reset(nand_1_out));  // open: preset
  Hex_Digit_Display hex_digit_display_1 (.value(cnt_up_mod16_1_q));  // open: dp
  cnt_up_mod16 cnt_up_mod16_1 (.clk(CLK_out), .z(Z_out), .q(cnt_up_mod16_1_q));
  D_Flip_Flop FF3 (.D(FF3_qn), .clk(FF2_qn), .Q(Q3), .Qn(FF3_qn), .reset(nand_1_out));  // open: preset
  Hex_Digit_Display hex_digit_display_2 (.value({Q3, Q2, Q1, Q0}));  // open: dp

  // Notes on the sheet:
  //   Botão simula a tecla Z - ativo baixo
endmodule

// VHDL entity dff, as the project stores it:
--------------------------------------------------------------------------------
-- UTFPR - Universidade Tecnológica Federal do Paraná - Curitiba - PR
-- Projeto  : Prática 5 - Cronômetro
-- Circuito : Implementação de um FF tipo D
-- Arquivo  : dff_vhdl.vhd
-- Autor    : prof. Gortan
-- Data     : Maio 2022
--------------------------------------------------------------------------------
-- Descrição :
-- Implementa um flip-flop tipo D para ser usado como componente em outros circ.
-- obs.: O Logisim-evolution 3.7.2 irá armazenar esse componente
--       em uma biblioteca do Modelsim contida em:
-- 
--       C:\users\<nome_usuário>\AppData\Local\Temp\logisim\sim\comp\work 
--     
--       O Logisim-evolution criará um componente nesse local com o nome
--       da entity seguido de underline, seguido do nome do rótulo ou label
--       atribuido ao componente no circuito.
--
--       Neste projeto:
--       	a entity para o flip-flop tipo D será: dff
--          o rótulo (label) usado para o componente no circuito será: vhdl
--       Consequentemente o logisim criará um componente chamado dff_vhdl
--
--       É possível verificar no diretório:
--       C:\users\<nome_usuário>\AppData\Local\Temp\logisim\sim\src
--       que o Logisim-evolution realmente modificou o nome
--       do arquivo para dff_vhdl.vhdl e da entity para dff_vhdl
--
--       Esse será portanto o nome do componente referenciado em todos os
--       demais circuitos que fizerem uso desse componente.
--
--       Ao exportar este arquivo para o Quartus lembrar de renomear a entity
--       para dff_vhdl para que possa ser referenciada pelos outros circuitos.
--
--       Atenção: O Logisim-evolution não apaga o conteúdo da biblioteca "work"
--                citada acima. 
--				  Isso pode tanto ajudar como atrapalhar novos projetos
--                (dependendo do conteúdo de projetos anteriores estar
--                ou não de acordo com as necessidades do projeto atual)
--                Por esse motivo é sempre aconselhável apagar essa bibioteca
--                "work" antes de iniciar um novo projeto e também apagar a
--                pasta    C:\users\<nome_usuário>\AppData\Local\Temp\work
--                usada pelo Logisim-evolution como uma especie de cache.
--       O professor apagará sempre essas duas pastas antes de iniciar a 
--       validação de trabalhos submetidos por alunos. Não deixe de fazer isso
--       também antes de realizar uma última verificação para postar seus trabalhos
--------------------------------------------------------------------------------

--============================= Módulo comps: ==================================
library ieee;
  use ieee.std_logic_1164.all;

--==================== Componente: =============================================
library ieee;
  use ieee.std_logic_1164.all;

entity dff is								-- nome da entity será alterado
  port(
    d, clk, prs, clr	: in  std_logic;	-- entradas: dado, clk, preset e clear
    q, qn				: out std_logic	-- saídas:   q e q invertido
 );
end dff;

architecture ff_d of dff is

	signal qstate: std_logic;

begin
	process(clk, clr, prs)
	begin
		if clr = '1' then qstate <= '0';	 -- clr tem prioridade
		elsif prs = '1' then qstate <= '1'; -- sobre prs
		elsif clk = '1' and clk' event then qstate <= d;
		end if;
	end process;
	q <= qstate;
	qn <= not qstate;
end ff_d;

// VHDL entity cnt_up_mod16, as the project stores it:
--------------------------------------------------------------------------------
-- UTFPR - Universidade Tecnológica Federal do Paraná - Curitiba - PR
-- Projeto  : Prática 5 - Cronômetro
-- Circuito : Contador assíncrono ascendente módulo 16
-- Arquivo  : cnt_up_mod16.vhd
-- Autor    : prof. Gortan
-- Data     : Maio 2022
--------------------------------------------------------------------------------
-- Descrição :
-- Implementa um contador assíncrono ascendente módulo 16
-- Utiliza ffs tipo D com resposta a flanco positivo do clock e clear e preset
-- assíncronos ativos em alto (componente dff referenciado como dff_vhdl)
--------------------------------------------------------------------------------

--============================= Nível Superior: =========================================
library ieee;
  use ieee.std_logic_1164.all;

entity cnt_up_mod16 is
  port(
    clk, z  : in  std_logic;					-- entradas clk, rst
    q       : out std_logic_vector(3 downto 0)	-- saída q3 até q0
 );
end cnt_up_mod16;

architecture cnt_up_mod16_arch of cnt_up_mod16 is
	signal zn: std_logic;
	signal qn: std_logic_vector(3 downto 0);	-- liga qn com d
	component dff_vhdl is					-- dff referenciado como dff_vhdl
		port
		(
			d, clk, prs, clr	: in  std_logic;	-- entradas: dado, clk, preset e clear
			q, qn			: out std_logic 	-- saídas:   q e q invertido
		);
	end component;
begin
	zn <= not z;
	ff_d0: dff_vhdl port map(d => qn(0), prs => '0', clr => zn, clk => clk,   q => q(0), qn => qn(0));
	ff_d1: dff_vhdl port map(d => qn(1), prs => '0', clr => zn, clk => qn(0), q => q(1), qn => qn(1));
	ff_d2: dff_vhdl port map(d => qn(2), prs => '0', clr => zn, clk => qn(1), q => q(2), qn => qn(2));
	ff_d3: dff_vhdl port map(d => qn(3), prs => '0', clr => zn, clk => qn(2), q => q(3), qn => qn(3));

end cnt_up_mod16_arch;

// VHDL entity P2_cnt_up_mod10_vhdl, as the project stores it:
library ieee;
  use ieee.std_logic_1164.all;

entity P2_cnt_up_mod10_vhdl is
  port(
    clk, z  : in  std_logic;					
    q       : out std_logic_vector(3 downto 0)	
 );
end P2_cnt_up_mod10_vhdl;

architecture cnt_up_mod10_arch of P2_cnt_up_mod10_vhdl is
	signal zn: std_logic;
	signal qn: std_logic_vector(3 downto 0);
	signal qstate: std_logic_vector(3 downto 0);
	component dff_vhdl is					
		port
		(
			d, clk, prs, clr	: in  std_logic;	
			q, qn			: out std_logic 	
		);
	end component;
begin
	zn <= not(z and not(qstate(1) and qstate(3)));
	ff_d0: dff_vhdl port map(d => qn(0), prs => '0', clr => zn, clk => clk,   q => qstate(0), qn => qn(0));
	ff_d1: dff_vhdl port map(d => qn(1), prs => '0', clr => zn, clk => qn(0), q => qstate(1), qn => qn(1));
	ff_d2: dff_vhdl port map(d => qn(2), prs => '0', clr => zn, clk => qn(1), q => qstate(2), qn => qn(2));
	ff_d3: dff_vhdl port map(d => qn(3), prs => '0', clr => zn, clk => qn(2), q => qstate(3), qn => qn(3));
	q(0) <= qstate(0);
	q(1) <= qstate(1);
	q(2) <= qstate(2);
	q(3) <= qstate(3);
end cnt_up_mod10_arch;
