// Logisim project Lab_05_P1_info.circ as structural Verilog
module componentes (
);

  dff vhdl ();  // open: d, clk, prs, clr, q, qn

  // Notes on the sheet:
  //   Este era o circuito "main"
  //   Caso o componente não receba um rótulo,
  //   Foi renomeado para "componentes"
  //   para lembrar que armazena os componentes VHDL
  //   O componente "dff" recebeu o rótulo (label) "vhdl" (em azul)
  //   para que o o Logisim o renomeie para "dff_vhdl"
  //   o Logisim utilizará um rótulo padrão tipo "component_0",
  //   o que dificultará sua utilização em outros circuitos deste projeto
  //   Para que a utilização deste (e outros possíveis) componentes
  //   nos passos seguintes seja bem sucedida, é preciso  que o componente
  //   já tenha sido previamente compilado, ou não será reconhecido pelo Logisim
  //   Os demais circuitos deverão referenciar esse componente portanto como "dff_vhdl"
endmodule

module P1_cnt_up_mod16 (
);

  wire CLK_out, FF0_qn, FF1_qn, FF2_qn, FF3_qn, not_1_out, Q0, Q1, Q2, Q3, Z_out;
  wire [3:0] p1_cnt_up_mod16_vhdl_1_q;

  Clock CLK (.out(CLK_out));
  Button #(.press("passive")) Z (.out(Z_out));
  D_Flip_Flop FF0 (.D(FF0_qn), .clk(CLK_out), .Q(Q0), .Qn(FF0_qn), .reset(not_1_out));  // open: preset
  not not_1 (not_1_out, Z_out);
  D_Flip_Flop FF1 (.D(FF1_qn), .clk(FF0_qn), .Q(Q1), .Qn(FF1_qn), .reset(not_1_out));  // open: preset
  D_Flip_Flop FF2 (.D(FF2_qn), .clk(FF1_qn), .Q(Q2), .Qn(FF2_qn), .reset(not_1_out));  // open: preset
  Hex_Digit_Display hex_digit_display_1 (.value(p1_cnt_up_mod16_vhdl_1_q));  // open: dp
  P1_cnt_up_mod16_vhdl p1_cnt_up_mod16_vhdl_1 (.clk(CLK_out), .z(Z_out), .q(p1_cnt_up_mod16_vhdl_1_q));
  D_Flip_Flop FF3 (.D(FF3_qn), .clk(FF2_qn), .Q(Q3), .Qn(FF3_qn), .reset(not_1_out));  // open: preset
  Hex_Digit_Display hex_digit_display_2 (.value({Q3, Q2, Q1, Q0}));  // open: dp

  // Notes on the sheet:
  //   Botão simula a tecla Z - ativo baixo
endmodule

module P2_cnt_up_mod10 (
);

  wire CLK_out, FF0_qn, FF1_qn, FF2_qn, FF3_qn, nand_1_out, nand_2_out, Q0, Q1, Q2, Q3, Z_out;
  wire [3:0] p2_cnt_up_mod10_vhdl_1_q;

  Clock CLK (.out(CLK_out));
  Button #(.press("passive")) Z (.out(Z_out));
  nand nand_1 (nand_1_out, nand_2_out, Z_out);
  D_Flip_Flop FF0 (.D(FF0_qn), .clk(CLK_out), .Q(Q0), .Qn(FF0_qn), .reset(nand_1_out));  // open: preset
  nand nand_2 (nand_2_out, Q3, Q1);
  D_Flip_Flop FF1 (.D(FF1_qn), .clk(FF0_qn), .Q(Q1), .Qn(FF1_qn), .reset(nand_1_out));  // open: preset
  D_Flip_Flop FF2 (.D(FF2_qn), .clk(FF1_qn), .Q(Q2), .Qn(FF2_qn), .reset(nand_1_out));  // open: preset
  Hex_Digit_Display hex_digit_display_1 (.value(p2_cnt_up_mod10_vhdl_1_q));  // open: dp
  P2_cnt_up_mod10_vhdl p2_cnt_up_mod10_vhdl_1 (.clk(CLK_out), .z(Z_out), .q(p2_cnt_up_mod10_vhdl_1_q));
  D_Flip_Flop FF3 (.D(FF3_qn), .clk(FF2_qn), .Q(Q3), .Qn(FF3_qn), .reset(nand_1_out));  // open: preset
  Hex_Digit_Display hex_digit_display_2 (.value({Q3, Q2, Q1, Q0}));  // open: dp
endmodule

module P3_cnt_up_mod10_alargador (
);

  wire CLK_out, d_ff_1_q, FF0_qn, FF1_qn, FF2_qn, FF3_qn, nand_1_out, nand_2_out, not_1_out, Q0, Q1, Q2, Q3,
       Z_out;
  wire [3:0] p3_cnt_up_mod10_alargador_vhdl_1_q;

  Clock CLK (.out(CLK_out));
  Button #(.press("passive")) Z (.out(Z_out));
  nand nand_1 (nand_1_out, nand_2_out, Z_out);
  D_Flip_Flop FF0 (.D(FF0_qn), .clk(CLK_out), .Q(Q0), .Qn(FF0_qn), .reset(d_ff_1_q));  // open: preset
  not not_1 (not_1_out, CLK_out);
  nand nand_2 (nand_2_out, Q3, Q1);
  D_Flip_Flop FF1 (.D(FF1_qn), .clk(FF0_qn), .Q(Q1), .Qn(FF1_qn), .reset(d_ff_1_q));  // open: preset
  D_Flip_Flop d_ff_1 (.Q(d_ff_1_q), .preset(nand_1_out), .reset(not_1_out));  // open: D, clk, Qn
  D_Flip_Flop FF2 (.D(FF2_qn), .clk(FF1_qn), .Q(Q2), .Qn(FF2_qn), .reset(d_ff_1_q));  // open: preset
  Hex_Digit_Display hex_digit_display_1 (.value(p3_cnt_up_mod10_alargador_vhdl_1_q));  // open: dp
  P3_cnt_up_mod10_alargador_vhdl p3_cnt_up_mod10_alargador_vhdl_1 (
    .clk(CLK_out), .z(Z_out), .q(p3_cnt_up_mod10_alargador_vhdl_1_q));
  D_Flip_Flop FF3 (.D(FF3_qn), .clk(FF2_qn), .Q(Q3), .Qn(FF3_qn), .reset(d_ff_1_q));  // open: preset
  Hex_Digit_Display hex_digit_display_2 (.value({Q3, Q2, Q1, Q0}));  // open: dp
endmodule

module P4_cnt_up_mod6 (
);

  wire CLK_out, FF0_qn, FF1_qn, FF2_qn, nand_1_out, nand_2_out, Q0, Q1, Q2, Z_out;
  wire [2:0] p4_cnt_up_mod6_vhdl_1_q;
  wire [3:3] p4_cnt_up_mod6_vhdl_1_q_2;

  Clock CLK (.out(CLK_out));
  Button #(.press("passive")) Z (.out(Z_out));
  nand nand_1 (nand_1_out, nand_2_out, Z_out);
  D_Flip_Flop FF0 (.D(FF0_qn), .clk(CLK_out), .Q(Q0), .Qn(FF0_qn), .reset(nand_1_out));  // open: preset
  nand nand_2 (nand_2_out, Q2, Q1);
  D_Flip_Flop FF1 (.D(FF1_qn), .clk(FF0_qn), .Q(Q1), .Qn(FF1_qn), .reset(nand_1_out));  // open: preset
  D_Flip_Flop FF2 (.D(FF2_qn), .clk(FF1_qn), .Q(Q2), .Qn(FF2_qn), .reset(nand_1_out));  // open: preset
  Hex_Digit_Display hex_digit_display_1 (.value({1'b0, p4_cnt_up_mod6_vhdl_1_q}));  // open: dp
  P4_cnt_up_mod6_vhdl p4_cnt_up_mod6_vhdl_1 (
    .clk(CLK_out), .z(Z_out), .q({p4_cnt_up_mod6_vhdl_1_q_2[3], p4_cnt_up_mod6_vhdl_1_q}));
  Hex_Digit_Display hex_digit_display_2 (.value({1'b0, Q2, Q1, Q0}));  // open: dp
  // Pins of 3 and 4 bits meet at {p4_cnt_up_mod6_vhdl_1_q_2[3], p4_cnt_up_mod6_vhdl_1_q}
endmodule

module P5_cnt_up_mod6_alargador (
);

  wire CLK_out, d_ff_1_q, FF0_qn, FF1_qn, FF2_qn, FF3_qn, nand_1_out, nand_2_out, not_1_out, Q0, Q1, Q2, Q3,
       Z_out;
  wire [3:0] p5_cnt_up_mod6_alargador_vhdl_1_q;

  Clock CLK (.out(CLK_out));
  Button #(.press("passive")) Z (.out(Z_out));
  nand nand_1 (nand_1_out, nand_2_out, Z_out);
  D_Flip_Flop FF0 (.D(FF0_qn), .clk(CLK_out), .Q(Q0), .Qn(FF0_qn), .reset(d_ff_1_q));  // open: preset
  not not_1 (not_1_out, CLK_out);
  nand nand_2 (nand_2_out, Q2, Q1);
  D_Flip_Flop FF1 (.D(FF1_qn), .clk(FF0_qn), .Q(Q1), .Qn(FF1_qn), .reset(d_ff_1_q));  // open: preset
  D_Flip_Flop d_ff_1 (.Q(d_ff_1_q), .preset(nand_1_out), .reset(not_1_out));  // open: D, clk, Qn
  D_Flip_Flop FF2 (.D(FF2_qn), .clk(FF1_qn), .Q(Q2), .Qn(FF2_qn), .reset(d_ff_1_q));  // open: preset
  Hex_Digit_Display hex_digit_display_1 (.value(p5_cnt_up_mod6_alargador_vhdl_1_q));  // open: dp
  P5_cnt_up_mod6_alargador_vhdl p5_cnt_up_mod6_alargador_vhdl_1 (
    .clk(CLK_out), .z(Z_out), .q(p5_cnt_up_mod6_alargador_vhdl_1_q));
  D_Flip_Flop FF3 (.D(FF3_qn), .clk(FF2_qn), .Q(Q3), .Qn(FF3_qn), .reset(d_ff_1_q));  // open: preset
  Hex_Digit_Display hex_digit_display_2 (.value({Q3, Q2, Q1, Q0}));  // open: dp
endmodule

module P6_cnt_down_mod16 (
);

  wire CLK_out, FF0_qn, FF1_qn, FF2_qn, FF3_qn, not_1_out, Q0, Q1, Q2, Q3, Z_out;
  wire [3:0] not_2_out, p6_cnt_down_mod16_vhdl_1_q;

  Clock CLK (.out(CLK_out));
  Button #(.press("passive")) Z (.out(Z_out));
  D_Flip_Flop FF0 (.D(FF0_qn), .clk(CLK_out), .Q(Q0), .Qn(FF0_qn), .reset(not_1_out));  // open: preset
  not not_1 (not_1_out, Z_out);
  D_Flip_Flop FF1 (.D(FF1_qn), .clk(FF0_qn), .Q(Q1), .Qn(FF1_qn), .reset(not_1_out));  // open: preset
  D_Flip_Flop FF2 (.D(FF2_qn), .clk(FF1_qn), .Q(Q2), .Qn(FF2_qn), .reset(not_1_out));  // open: preset
  Hex_Digit_Display hex_digit_display_1 (.value(p6_cnt_down_mod16_vhdl_1_q));  // open: dp
  P6_cnt_down_mod16_vhdl p6_cnt_down_mod16_vhdl_1 (.clk(CLK_out), .z(Z_out), .q(p6_cnt_down_mod16_vhdl_1_q));
  D_Flip_Flop FF3 (.D(FF3_qn), .clk(FF2_qn), .Q(Q3), .Qn(FF3_qn), .reset(not_1_out));  // open: preset
  Hex_Digit_Display hex_digit_display_2 (.value(not_2_out));  // open: dp
  not not_2 (not_2_out[0], Q0);
  not not_3 (not_2_out[1], Q1);
  not not_4 (not_2_out[2], Q2);
  not not_5 (not_2_out[3], Q3);
endmodule

module P7_cnt_down_mod10 (
);

  wire and_1_out, and_2_out, CLK_out, d_ff_1_qn, d_ff_2_qn, d_ff_3_qn, d_ff_4_qn, d_ff_5_q, nor_1_out,
       not_1_out, or_1_out, Q0, Q1, Q2, Q3, Z_out;
  wire [3:0] p7_cnt_down_mod10_vhdl_1_q;

  Clock CLK (.out(CLK_out));
  Button #(.press("passive")) Z (.out(Z_out));
  D_Flip_Flop d_ff_1 (.D(d_ff_1_qn), .clk(CLK_out), .Q(Q0), .Qn(d_ff_1_qn), .preset(or_1_out));  // open: reset
  not not_1 (not_1_out, Z_out);
  D_Flip_Flop d_ff_2 (.D(d_ff_2_qn), .clk(Q0), .Q(Q1), .Qn(d_ff_2_qn), .reset(or_1_out));  // open: preset
  D_Flip_Flop d_ff_3 (.D(d_ff_3_qn), .clk(Q1), .Q(Q2), .Qn(d_ff_3_qn), .reset(or_1_out));  // open: preset
  P7_cnt_down_mod10_vhdl p7_cnt_down_mod10_vhdl_1 (.clk(CLK_out), .z(Z_out), .q(p7_cnt_down_mod10_vhdl_1_q));
  Hex_Digit_Display hex_digit_display_1 (.value(p7_cnt_down_mod10_vhdl_1_q));  // open: dp
  Hex_Digit_Display hex_digit_display_2 (.value({Q3, Q2, Q1, Q0}));  // open: dp
  D_Flip_Flop d_ff_4 (.D(d_ff_4_qn), .clk(Q2), .Q(Q3), .Qn(d_ff_4_qn), .preset(or_1_out));  // open: reset
  and and_1 (and_1_out, Q0, Q1, Q2, Q3);
  nor nor_1 (nor_1_out, Q0, Q1, Q2, Q3);
  D_Flip_Flop d_ff_5 (.Q(d_ff_5_q), .preset(nor_1_out), .reset(or_1_out));  // open: D, clk, Qn
  or or_1 (or_1_out, and_2_out, not_1_out);
  and and_2 (and_2_out, and_1_out, d_ff_5_q);
endmodule

module P8_cnt_down_mod10_alargador (
);

  wire and_1_out, and_2_out, CLK_out, d_ff_1_qn, d_ff_2_qn, d_ff_3_q, d_ff_4_qn, d_ff_5_qn, d_ff_6_q,
       nor_1_out, not_1_out, not_2_out, or_1_out, Q0, Q1, Q2, Q3, Z_out;
  wire [3:0] p8_cnt_down_mod10_alargador_vhdl_1_q;

  Clock CLK (.out(CLK_out));
  Button #(.press("passive")) Z (.out(Z_out));
  D_Flip_Flop d_ff_1 (.D(d_ff_1_qn), .clk(CLK_out), .Q(Q0), .Qn(d_ff_1_qn), .preset(d_ff_3_q));  // open: reset
  not not_1 (not_1_out, Z_out);
  D_Flip_Flop d_ff_2 (.D(d_ff_2_qn), .clk(Q0), .Q(Q1), .Qn(d_ff_2_qn), .reset(d_ff_3_q));  // open: preset
  not not_2 (not_2_out, CLK_out);
  D_Flip_Flop d_ff_3 (.Q(d_ff_3_q), .preset(or_1_out), .reset(not_2_out));  // open: D, clk, Qn
  D_Flip_Flop d_ff_4 (.D(d_ff_4_qn), .clk(Q1), .Q(Q2), .Qn(d_ff_4_qn), .reset(d_ff_3_q));  // open: preset
  P8_cnt_down_mod10_alargador_vhdl p8_cnt_down_mod10_alargador_vhdl_1 (
    .clk(CLK_out), .z(Z_out), .q(p8_cnt_down_mod10_alargador_vhdl_1_q));
  Hex_Digit_Display hex_digit_display_1 (.value(p8_cnt_down_mod10_alargador_vhdl_1_q));  // open: dp
  Hex_Digit_Display hex_digit_display_2 (.value({Q3, Q2, Q1, Q0}));  // open: dp
  D_Flip_Flop d_ff_5 (.D(d_ff_5_qn), .clk(Q2), .Q(Q3), .Qn(d_ff_5_qn), .preset(d_ff_3_q));  // open: reset
  and and_1 (and_1_out, Q0, Q1, Q2, Q3);
  nor nor_1 (nor_1_out, Q0, Q1, Q2, Q3);
  D_Flip_Flop d_ff_6 (.Q(d_ff_6_q), .preset(nor_1_out), .reset(d_ff_3_q));  // open: D, clk, Qn
  and and_2 (and_2_out, and_1_out, d_ff_6_q);
  or or_1 (or_1_out, and_2_out, not_1_out);
endmodule

module P9_cnt_down_mod6 (
);

  wire and_1_out, and_2_out, CLK_out, d_ff_1_qn, d_ff_2_qn, d_ff_3_qn, d_ff_4_qn, d_ff_5_q, nor_1_out,
       not_1_out, or_1_out, Q0, Q1, Q2, Q3, Z_out;
  wire [3:0] p9_cnt_down_mod6_vhdl_1_q;

  Clock CLK (.out(CLK_out));
  Button #(.press("passive")) Z (.out(Z_out));
  D_Flip_Flop d_ff_1 (.D(d_ff_1_qn), .clk(CLK_out), .Q(Q0), .Qn(d_ff_1_qn), .preset(or_1_out));  // open: reset
  not not_1 (not_1_out, Z_out);
  D_Flip_Flop d_ff_2 (.D(d_ff_2_qn), .clk(Q0), .Q(Q1), .Qn(d_ff_2_qn), .reset(or_1_out));  // open: preset
  D_Flip_Flop d_ff_3 (.D(d_ff_3_qn), .clk(Q1), .Q(Q2), .Qn(d_ff_3_qn), .preset(or_1_out));  // open: reset
  P9_cnt_down_mod6_vhdl p9_cnt_down_mod6_vhdl_1 (.clk(CLK_out), .z(Z_out), .q(p9_cnt_down_mod6_vhdl_1_q));
  Hex_Digit_Display hex_digit_display_1 (.value(p9_cnt_down_mod6_vhdl_1_q));  // open: dp
  Hex_Digit_Display hex_digit_display_2 (.value({Q3, Q2, Q1, Q0}));  // open: dp
  D_Flip_Flop d_ff_4 (.D(d_ff_4_qn), .clk(Q2), .Q(Q3), .Qn(d_ff_4_qn), .reset(or_1_out));  // open: preset
  and and_1 (and_1_out, Q0, Q1, Q2, Q3);
  nor nor_1 (nor_1_out, Q0, Q1, Q2, Q3);
  D_Flip_Flop d_ff_5 (.Q(d_ff_5_q), .preset(nor_1_out), .reset(or_1_out));  // open: D, clk, Qn
  or or_1 (or_1_out, and_2_out, not_1_out);
  and and_2 (and_2_out, and_1_out, d_ff_5_q);
endmodule

module P10_cnt_down_mod6_alargador (
);

  wire and_1_out, and_2_out, CLK_out, d_ff_1_qn, d_ff_2_qn, d_ff_3_q, d_ff_4_qn, d_ff_5_qn, d_ff_6_q,
       nor_1_out, not_1_out, not_2_out, or_1_out, Q0, Q1, Q2, Q3, Z_out;
  wire [3:0] p10_cnt_down_mod6_alargador_vhdl_1_q;

  Clock CLK (.out(CLK_out));
  Button #(.press("passive")) Z (.out(Z_out));
  D_Flip_Flop d_ff_1 (.D(d_ff_1_qn), .clk(CLK_out), .Q(Q0), .Qn(d_ff_1_qn), .preset(d_ff_3_q));  // open: reset
  not not_1 (not_1_out, Z_out);
  D_Flip_Flop d_ff_2 (.D(d_ff_2_qn), .clk(Q0), .Q(Q1), .Qn(d_ff_2_qn), .reset(d_ff_3_q));  // open: preset
  not not_2 (not_2_out, CLK_out);
  D_Flip_Flop d_ff_3 (.Q(d_ff_3_q), .preset(or_1_out), .reset(not_2_out));  // open: D, clk, Qn
  D_Flip_Flop d_ff_4 (.D(d_ff_4_qn), .clk(Q1), .Q(Q2), .Qn(d_ff_4_qn), .preset(d_ff_3_q));  // open: reset
  P10_cnt_down_mod6_alargador_vhdl p10_cnt_down_mod6_alargador_vhdl_1 (
    .clk(CLK_out), .z(Z_out), .q(p10_cnt_down_mod6_alargador_vhdl_1_q));
  Hex_Digit_Display hex_digit_display_1 (.value(p10_cnt_down_mod6_alargador_vhdl_1_q));  // open: dp
  Hex_Digit_Display hex_digit_display_2 (.value({Q3, Q2, Q1, Q0}));  // open: dp
  D_Flip_Flop d_ff_5 (.D(d_ff_5_qn), .clk(Q2), .Q(Q3), .Qn(d_ff_5_qn), .reset(d_ff_3_q));  // open: preset
  and and_1 (and_1_out, Q0, Q1, Q2, Q3);
  nor nor_1 (nor_1_out, Q0, Q1, Q2, Q3);
  D_Flip_Flop d_ff_6 (.Q(d_ff_6_q), .preset(nor_1_out), .reset(d_ff_3_q));  // open: D, clk, Qn
  and and_2 (and_2_out, and_1_out, d_ff_6_q);
  or or_1 (or_1_out, and_2_out, not_1_out);
endmodule

module P11_cnt_up_down_mod10 (
  input  UD
);

  wire and_1_out, and_2_out, CLK, d_ff_1_qn, d_ff_2_qn, d_ff_3_q, d_ff_4_qn, d_ff_5_q, d_ff_6_qn, d_ff_7_qn,
       d_ff_8_qn, d_ff_9_qn, d_ff_10_qn, d_ff_11_q, nand_1_out, nand_2_out, nor_1_out, not_1_out, not_2_out,
       not_3_out, or_1_out, Z;
  wire [3:0] d_ff_1_q, d_ff_2_q, multiplexer_1_out, p11_cnt_up_down_mod10_vhdl_1_q;

  Clock u_CLK (.out(CLK));
  Button #(.press("passive")) u_Z (.out(Z));
  nand nand_1 (nand_1_out, nand_2_out, Z);
  D_Flip_Flop d_ff_1 (.D(d_ff_1_qn), .clk(CLK), .Q(d_ff_1_q[0]), .Qn(d_ff_1_qn), .preset(d_ff_3_q));  // open: reset
  not not_1 (not_1_out, Z);
  not not_2 (not_2_out, CLK);
  D_Flip_Flop d_ff_2 (.D(d_ff_2_qn), .clk(CLK), .Q(d_ff_2_q[0]), .Qn(d_ff_2_qn), .reset(d_ff_5_q));  // open: preset
  not not_3 (not_3_out, CLK);
  D_Flip_Flop d_ff_3 (.Q(d_ff_3_q), .preset(or_1_out), .reset(not_2_out));  // open: D, clk, Qn
  nand nand_2 (nand_2_out, d_ff_2_q[3], d_ff_2_q[1]);
  D_Flip_Flop d_ff_4 (
    .D(d_ff_4_qn), .clk(d_ff_2_qn), .Q(d_ff_2_q[1]), .Qn(d_ff_4_qn), .reset(d_ff_5_q));  // open: preset
  D_Flip_Flop d_ff_5 (.Q(d_ff_5_q), .preset(nand_1_out), .reset(not_3_out));  // open: D, clk, Qn
  D_Flip_Flop d_ff_6 (
    .D(d_ff_6_qn), .clk(d_ff_1_q[0]), .Q(d_ff_1_q[1]), .Qn(d_ff_6_qn), .reset(d_ff_3_q));  // open: preset
  D_Flip_Flop d_ff_7 (
    .D(d_ff_7_qn), .clk(d_ff_1_q[1]), .Q(d_ff_1_q[2]), .Qn(d_ff_7_qn), .reset(d_ff_3_q));  // open: preset
  D_Flip_Flop d_ff_8 (
    .D(d_ff_8_qn), .clk(d_ff_4_qn), .Q(d_ff_2_q[2]), .Qn(d_ff_8_qn), .reset(d_ff_5_q));  // open: preset
  D_Flip_Flop d_ff_9 (
    .D(d_ff_9_qn), .clk(d_ff_8_qn), .Q(d_ff_2_q[3]), .Qn(d_ff_9_qn), .reset(d_ff_5_q));  // open: preset
  D_Flip_Flop d_ff_10 (
    .D(d_ff_10_qn), .clk(d_ff_1_q[2]), .Q(d_ff_1_q[3]), .Qn(d_ff_10_qn), .preset(d_ff_3_q));  // open: reset
  Multiplexer #(.width(4)) multiplexer_1 (.in0(d_ff_2_q), .in1(d_ff_1_q), .out(multiplexer_1_out), .sel(UD));
  and and_1 (and_1_out, d_ff_1_q[0], d_ff_1_q[1], d_ff_1_q[2], d_ff_1_q[3]);
  nor nor_1 (nor_1_out, d_ff_1_q[0], d_ff_1_q[1], d_ff_1_q[2], d_ff_1_q[3]);
  D_Flip_Flop d_ff_11 (.Q(d_ff_11_q), .preset(nor_1_out), .reset(d_ff_3_q));  // open: D, clk, Qn
  Hex_Digit_Display hex_digit_display_1 (.value(multiplexer_1_out));  // open: dp
  and and_2 (and_2_out, and_1_out, d_ff_11_q);
  or or_1 (or_1_out, and_2_out, not_1_out);
  Hex_Digit_Display hex_digit_display_2 (.value(p11_cnt_up_down_mod10_vhdl_1_q));  // open: dp
  P11_cnt_up_down_mod10_vhdl p11_cnt_up_down_mod10_vhdl_1 (
    .clk(CLK), .z(Z), .ud(UD), .q(p11_cnt_up_down_mod10_vhdl_1_q));  // open: co
endmodule

module P12_cnt_up_down_mod6 (
  input  UD
);

  wire and_1_out, and_2_out, CLK, d_ff_1_qn, d_ff_2_qn, d_ff_3_q, d_ff_4_qn, d_ff_5_q, d_ff_6_qn, d_ff_7_qn,
       d_ff_8_qn, d_ff_9_qn, d_ff_10_qn, d_ff_11_q, nand_1_out, nand_2_out, nor_1_out, not_1_out, not_2_out,
       not_3_out, or_1_out, Z;
  wire [3:0] d_ff_1_q, d_ff_2_q, multiplexer_1_out, p12_cnt_up_down_mod6_vhdl_1_q;

  Clock u_CLK (.out(CLK));
  Button #(.press("passive")) u_Z (.out(Z));
  nand nand_1 (nand_1_out, nand_2_out, Z);
  D_Flip_Flop d_ff_1 (.D(d_ff_1_qn), .clk(CLK), .Q(d_ff_1_q[0]), .Qn(d_ff_1_qn), .preset(d_ff_3_q));  // open: reset
  not not_1 (not_1_out, Z);
  not not_2 (not_2_out, CLK);
  D_Flip_Flop d_ff_2 (.D(d_ff_2_qn), .clk(CLK), .Q(d_ff_2_q[0]), .Qn(d_ff_2_qn), .reset(d_ff_5_q));  // open: preset
  not not_3 (not_3_out, CLK);
  D_Flip_Flop d_ff_3 (.Q(d_ff_3_q), .preset(or_1_out), .reset(not_2_out));  // open: D, clk, Qn
  nand nand_2 (nand_2_out, d_ff_2_q[2], d_ff_2_q[1]);
  D_Flip_Flop d_ff_4 (
    .D(d_ff_4_qn), .clk(d_ff_2_qn), .Q(d_ff_2_q[1]), .Qn(d_ff_4_qn), .reset(d_ff_5_q));  // open: preset
  D_Flip_Flop d_ff_5 (.Q(d_ff_5_q), .preset(nand_1_out), .reset(not_3_out));  // open: D, clk, Qn
  D_Flip_Flop d_ff_6 (
    .D(d_ff_6_qn), .clk(d_ff_1_q[0]), .Q(d_ff_1_q[1]), .Qn(d_ff_6_qn), .reset(d_ff_3_q));  // open: preset
  D_Flip_Flop d_ff_7 (
    .D(d_ff_7_qn), .clk(d_ff_1_q[1]), .Q(d_ff_1_q[2]), .Qn(d_ff_7_qn), .preset(d_ff_3_q));  // open: reset
  D_Flip_Flop d_ff_8 (
    .D(d_ff_8_qn), .clk(d_ff_4_qn), .Q(d_ff_2_q[2]), .Qn(d_ff_8_qn), .reset(d_ff_5_q));  // open: preset
  D_Flip_Flop d_ff_9 (
    .D(d_ff_9_qn), .clk(d_ff_8_qn), .Q(d_ff_2_q[3]), .Qn(d_ff_9_qn), .reset(d_ff_5_q));  // open: preset
  D_Flip_Flop d_ff_10 (
    .D(d_ff_10_qn), .clk(d_ff_1_q[2]), .Q(d_ff_1_q[3]), .Qn(d_ff_10_qn), .reset(d_ff_3_q));  // open: preset
  Multiplexer #(.width(4)) multiplexer_1 (.in0(d_ff_2_q), .in1(d_ff_1_q), .out(multiplexer_1_out), .sel(UD));
  and and_1 (and_1_out, d_ff_1_q[0], d_ff_1_q[1], d_ff_1_q[2], d_ff_1_q[3]);
  nor nor_1 (nor_1_out, d_ff_1_q[0], d_ff_1_q[1], d_ff_1_q[2], d_ff_1_q[3]);
  D_Flip_Flop d_ff_11 (.Q(d_ff_11_q), .preset(nor_1_out), .reset(d_ff_3_q));  // open: D, clk, Qn
  Hex_Digit_Display hex_digit_display_1 (.value(multiplexer_1_out));  // open: dp
  and and_2 (and_2_out, and_1_out, d_ff_11_q);
  or or_1 (or_1_out, and_2_out, not_1_out);
  Hex_Digit_Display hex_digit_display_2 (.value(p12_cnt_up_down_mod6_vhdl_1_q));  // open: dp
  P12_cnt_up_down_mod6_vhdl p12_cnt_up_down_mod6_vhdl_1 (.clk(CLK), .z(Z), .ud(UD), .q(p12_cnt_up_down_mod6_vhdl_1_q));
endmodule

module P13_cnt_up_down_mod60 (
  input  UD
);

  wire and_1_out, CLK_out, FF_SST_q, FF_SST_qn, not_1_out, p11_cnt_up_down_mod10_vhdl_1_co, SST_out, Z_out;
  wire [3:0] p11_cnt_up_down_mod10_vhdl_1_q, p12_cnt_up_down_mod6_vhdl_1_q, p13_cnt_up_down_mod60_vhdl_1_qd,
       p13_cnt_up_down_mod60_vhdl_1_qu;

  Button SST (.out(SST_out));
  Clock CLK (.out(CLK_out));
  Button #(.press("passive")) Z (.out(Z_out));
  D_Flip_Flop FF_SST (.D(FF_SST_qn), .clk(SST_out), .Q(FF_SST_q), .Qn(FF_SST_qn), .reset(not_1_out));  // open: preset
  not not_1 (not_1_out, Z_out);
  and and_1 (and_1_out, FF_SST_q, CLK_out);
  P11_cnt_up_down_mod10_vhdl p11_cnt_up_down_mod10_vhdl_1 (
    .clk(and_1_out), .z(Z_out), .ud(UD), .q(p11_cnt_up_down_mod10_vhdl_1_q),
    .co(p11_cnt_up_down_mod10_vhdl_1_co));
  P12_cnt_up_down_mod6_vhdl p12_cnt_up_down_mod6_vhdl_1 (
    .clk(p11_cnt_up_down_mod10_vhdl_1_co), .z(Z_out), .ud(UD), .q(p12_cnt_up_down_mod6_vhdl_1_q));
  P13_cnt_up_down_mod60_vhdl p13_cnt_up_down_mod60_vhdl_1 (
    .clk(CLK_out), .z(Z_out), .ud(UD), .sst(SST_out), .qu(p13_cnt_up_down_mod60_vhdl_1_qu),
    .qd(p13_cnt_up_down_mod60_vhdl_1_qd));
  Hex_Digit_Display hex_digit_display_1 (.value(p12_cnt_up_down_mod6_vhdl_1_q));  // open: dp
  Hex_Digit_Display hex_digit_display_2 (.value(p11_cnt_up_down_mod10_vhdl_1_q));  // open: dp
  Hex_Digit_Display hex_digit_display_3 (.value(p13_cnt_up_down_mod60_vhdl_1_qd));  // open: dp
  Hex_Digit_Display hex_digit_display_4 (.value(p13_cnt_up_down_mod60_vhdl_1_qu));  // open: dp
endmodule

// VHDL entity dff, as the project stores it:
--------------------------------------------------------------------------------
-- UTFPR - Universidade Tecnológica Federal do Paraná - Curitiba - PR
-- Projeto  : Prática 5 - Cronômetro
-- Circuito : Implementação de um FF tipo D
-- Arquivo  : dff_vhdl.vhd
-- Autor    : prof. Gortan
-- Data     : Maio 2022
--------------------------------------------------------------------------------
-- Descrição :
-- Implementa um flip-flop tipo D para ser usado como componente em outros circ.
-- obs.: O Logisim-evolution 3.7.2 irá armazenar esse componente
--       em uma biblioteca do Modelsim contida em:
-- 
--       C:\users\<nome_usuário>\AppData\Local\Temp\logisim\sim\comp\work 
--     
--       O Logisim-evolution criará um componente nesse local com o nome
--       da entity seguido de underline, seguido do nome do rótulo ou label
--       atribuido ao componente no circuito.
--
--       Neste projeto:
--       	a entity para o flip-flop tipo D será: dff
--          o rótulo (label) usado para o componente no circuito será: vhdl
--       Consequentemente o logisim criará um componente chamado dff_vhdl
--
--       É possível verificar no diretório:
--       C:\users\<nome_usuário>\AppData\Local\Temp\logisim\sim\src
--       que o Logisim-evolution realmente modificou o nome
--       do arquivo para dff_vhdl.vhdl e da entity para dff_vhdl
--
--       Esse será portanto o nome do componente referenciado em todos os
--       demais circuitos que fizerem uso desse componente.
--
--       Ao exportar este arquivo para o Quartus lembrar de renomear a entity
--       para dff_vhdl para que possa ser referenciada pelos outros circuitos.
--
--       Atenção: O Logisim-evolution não apaga o conteúdo da biblioteca "work"
--                citada acima. 
--				  Isso pode tanto ajudar como atrapalhar novos projetos
--                (dependendo do conteúdo de projetos anteriores estar
--                ou não de acordo com as necessidades do projeto atual)
--                Por esse motivo é sempre aconselhável apagar essa bibioteca
--                "work" antes de iniciar um novo projeto e também apagar a
--                pasta    C:\users\<nome_usuário>\AppData\Local\Temp\work
--                usada pelo Logisim-evolution como uma especie de cache.
--       O professor apagará sempre essas duas pastas antes de iniciar a 
--       validação de trabalhos submetidos por alunos. Não deixe de fazer isso
--       também antes de realizar uma última verificação para postar seus trabalhos
--------------------------------------------------------------------------------

--============================= Módulo comps: ==================================
library ieee;
  use ieee.std_logic_1164.all;

entity dff is								-- nome da entity será alterado
  port(
    d, clk, prs, clr	: in  std_logic;	-- entradas: dado, clk, preset e clear
    q, qn				: out std_logic	-- saídas:   q e q invertido
 );
end dff;

architecture ff_d of dff is

	signal qstate: std_logic;

begin
	process(clk, clr, prs)
	begin
		if clr = '1' then qstate <= '0';	 -- clr tem prioridade
		elsif prs = '1' then qstate <= '1'; -- sobre prs
		elsif clk = '1' and clk' event then qstate <= d;
		end if;
	end process;
	q <= qstate;
	qn <= not qstate;
end ff_d;

// VHDL entity P1_cnt_up_mod16_vhdl, as the project stores it:
--------------------------------------------------------------------------------
-- UTFPR - Universidade Tecnológica Federal do Paraná - Curitiba - PR
-- Projeto  : Prática 5 - Cronômetro
-- Circuito : Contador assíncrono ascendente módulo 16
-- Arquivo  : cnt_up_mod16.vhd
-- Autor    : prof. Gortan
-- Data     : Maio 2022
--------------------------------------------------------------------------------
-- Descrição :
-- Implementa um contador assíncrono ascendente módulo 16
-- Utiliza ffs tipo D com resposta a flanco positivo do clock e clear e preset
-- assíncronos ativos em alto (componente dff referenciado como dff_vhdl)
--------------------------------------------------------------------------------

--============================= Nível Superior: =========================================
library ieee;
  use ieee.std_logic_1164.all;

entity P1_cnt_up_mod16_vhdl is
  port(
    clk, z  : in  std_logic;					-- entradas clk, rst
    q       : out std_logic_vector(3 downto 0)	-- saída q3 até q0
 );
end P1_cnt_up_mod16_vhdl;

architecture cnt_up_mod16_arch of P1_cnt_up_mod16_vhdl is
	signal zn: std_logic;
	signal qn: std_logic_vector(3 downto 0);	-- liga qn com d
	component dff_vhdl is					-- dff referenciado como dff_vhdl
		port
		(
			d, clk, prs, clr	: in  std_logic;	-- entradas: dado, clk, preset e clear
			q, qn			: out std_logic 	-- saídas:   q e q invertido
		);
	end component;
begin
	zn <= not z;
	ff_d0: dff_vhdl port map(d => qn(0), prs => '0', clr => zn, clk => clk,   q => q(0), qn => qn(0));
	ff_d1: dff_vhdl port map(d => qn(1), prs => '0', clr => zn, clk => qn(0), q => q(1), qn => qn(1));
	ff_d2: dff_vhdl port map(d => qn(2), prs => '0', clr => zn, clk => qn(1), q => q(2), qn => qn(2));
	ff_d3: dff_vhdl port map(d => qn(3), prs => '0', clr => zn, clk => qn(2), q => q(3), qn => qn(3));

end cnt_up_mod16_arch;

// VHDL entity P2_cnt_up_mod10_vhdl, as the project stores it:
library ieee;
  use ieee.std_logic_1164.all;

entity P2_cnt_up_mod10_vhdl is
  port(
    clk, z  : in  std_logic;					
    q       : out std_logic_vector(3 downto 0)	
 );
end P2_cnt_up_mod10_vhdl;

architecture cnt_up_mod10_arch of P2_cnt_up_mod10_vhdl is
	signal zn: std_logic;
	signal qn: std_logic_vector(3 downto 0);
	signal qstate: std_logic_vector(3 downto 0);
	component dff_vhdl is					
		port
		(
			d, clk, prs, clr	: in  std_logic;	
			q, qn			: out std_logic 	
		);
	end component;
begin
	zn <= not(z and not(qstate(1) and qstate(3)));
	ff_d0: dff_vhdl port map(d => qn(0), prs => '0', clr => zn, clk => clk,   q => qstate(0), qn => qn(0));
	ff_d1: dff_vhdl port map(d => qn(1), prs => '0', clr => zn, clk => qn(0), q => qstate(1), qn => qn(1));
	ff_d2: dff_vhdl port map(d => qn(2), prs => '0', clr => zn, clk => qn(1), q => qstate(2), qn => qn(2));
	ff_d3: dff_vhdl port map(d => qn(3), prs => '0', clr => zn, clk => qn(2), q => qstate(3), qn => qn(3));
	q(0) <= qstate(0);
	q(1) <= qstate(1);
	q(2) <= qstate(2);
	q(3) <= qstate(3);
end cnt_up_mod10_arch;

// VHDL entity P3_cnt_up_mod10_alargador_vhdl, as the project stores it:
library ieee;
  use ieee.std_logic_1164.all;

entity P3_cnt_up_mod10_alargador_vhdl is
  port(
    clk, z  : in  std_logic;					
    q       : out std_logic_vector(3 downto 0)	
 );
end P3_cnt_up_mod10_alargador_vhdl;

architecture cnt_up_mod10_alargador_arch of P3_cnt_up_mod10_alargador_vhdl is
	signal zn: std_logic;
	signal qn: std_logic_vector(3 downto 0);
	signal qstate: std_logic_vector(3 downto 0);
	signal clr_aux, prs_rst, clkn: std_logic;
	component dff_vhdl is					
		port
		(
			d, clk, prs, clr	: in  std_logic;	
			q, qn			: out std_logic 	
		);
	end component;
begin
	zn <= clr_aux;
	clkn <= not clk;
	prs_rst <= ((not z) or (qstate(1) and qstate(3)));
	ff_d0: dff_vhdl port map(d => qn(0), prs => '0', clr => zn, clk => clk,   q => qstate(0), qn => qn(0));
	ff_d1: dff_vhdl port map(d => qn(1), prs => '0', clr => zn, clk => qn(0), q => qstate(1), qn => qn(1));
	ff_d2: dff_vhdl port map(d => qn(2), prs => '0', clr => zn, clk => qn(1), q => qstate(2), qn => qn(2));
	ff_d3: dff_vhdl port map(d => qn(3), prs => '0', clr => zn, clk => qn(2), q => qstate(3), qn => qn(3));
	ff_rst: dff_vhdl port map(d => '0', prs => prs_rst, clr => clkn, clk => '0', q => clr_aux);
	q(0) <= qstate(0);
	q(1) <= qstate(1);
	q(2) <= qstate(2);
	q(3) <= qstate(3);
end cnt_up_mod10_alargador_arch;

// VHDL entity P4_cnt_up_mod6_vhdl, as the project stores it:
library ieee;
  use ieee.std_logic_1164.all;

entity P4_cnt_up_mod6_vhdl is
  port(
    clk, z  : in  std_logic;					
    q       : out std_logic_vector(3 downto 0)	
 );
end P4_cnt_up_mod6_vhdl;

architecture cnt_up_mod6_arch of P4_cnt_up_mod6_vhdl is
	signal zn: std_logic;
	signal qn: std_logic_vector(3 downto 0);
	signal qstate: std_logic_vector(3 downto 0);
	component dff_vhdl is					
		port
		(
			d, clk, prs, clr	: in  std_logic;	
			q, qn			: out std_logic 	
		);
	end component;
begin
	zn <= not(z and not(qstate(1) and qstate(2)));
	ff_d0: dff_vhdl port map(d => qn(0), prs => '0', clr => zn, clk => clk,   q => qstate(0), qn => qn(0));
	ff_d1: dff_vhdl port map(d => qn(1), prs => '0', clr => zn, clk => qn(0), q => qstate(1), qn => qn(1));
	ff_d2: dff_vhdl port map(d => qn(2), prs => '0', clr => zn, clk => qn(1), q => qstate(2), qn => qn(2));
	ff_d3: dff_vhdl port map(d => qn(3), prs => '0', clr => zn, clk => qn(2), q => qstate(3), qn => qn(3));
	q(0) <= qstate(0);
	q(1) <= qstate(1);
	q(2) <= qstate(2);
	q(3) <= qstate(3);
end cnt_up_mod6_arch;

// VHDL entity P5_cnt_up_mod6_alargador_vhdl, as the project stores it:
library ieee;
  use ieee.std_logic_1164.all;

entity P5_cnt_up_mod6_alargador_vhdl is
  port(
    clk, z  : in  std_logic;					
    q       : out std_logic_vector(3 downto 0)	
 );
end P5_cnt_up_mod6_alargador_vhdl;

architecture cnt_up_mod6_alargador_arch of P5_cnt_up_mod6_alargador_vhdl is
	signal zn: std_logic;
	signal qn: std_logic_vector(3 downto 0);
	signal qstate: std_logic_vector(3 downto 0);
	signal clr_aux, prs_rst, clkn: std_logic;
	component dff_vhdl is					
		port
		(
			d, clk, prs, clr	: in  std_logic;	
			q, qn			: out std_logic 	
		);
	end component;
begin
	zn <= clr_aux;
	clkn <= not clk;
	prs_rst <= ((not z) or (qstate(1) and qstate(2)));
	ff_d0: dff_vhdl port map(d => qn(0), prs => '0', clr => zn, clk => clk,   q => qstate(0), qn => qn(0));
	ff_d1: dff_vhdl port map(d => qn(1), prs => '0', clr => zn, clk => qn(0), q => qstate(1), qn => qn(1));
	ff_d2: dff_vhdl port map(d => qn(2), prs => '0', clr => zn, clk => qn(1), q => qstate(2), qn => qn(2));
	ff_d3: dff_vhdl port map(d => qn(3), prs => '0', clr => zn, clk => qn(2), q => qstate(3), qn => qn(3));
	ff_rst: dff_vhdl port map(d => '0', prs => prs_rst, clr => clkn, clk => '0', q => clr_aux);
	q(0) <= qstate(0);
	q(1) <= qstate(1);
	q(2) <= qstate(2);
	q(3) <= qstate(3);
end cnt_up_mod6_alargador_arch;

// VHDL entity P6_cnt_down_mod16_vhdl, as the project stores it:
library ieee;
  use ieee.std_logic_1164.all;

entity P6_cnt_down_mod16_vhdl is
  port(
    clk, z  : in  std_logic;					
    q       : out std_logic_vector(3 downto 0)	
 );
end P6_cnt_down_mod16_vhdl;

architecture cnt_down_mod16_arch of P6_cnt_down_mod16_vhdl is
	signal zn: std_logic;
	signal qn: std_logic_vector(3 downto 0);	
	signal qstate: std_logic_vector(3 downto 0);
	component dff_vhdl is					
		port
		(
			d, clk, prs, clr	: in  std_logic;	
			q, qn			: out std_logic 	
		);
	end component;
begin
	zn <= not z;
	ff_d0: dff_vhdl port map(d => qn(0), prs => '0', clr => zn, clk => clk,   q => qstate(0), qn => qn(0));
	ff_d1: dff_vhdl port map(d => qn(1), prs => '0', clr => zn, clk => qn(0), q => qstate(1), qn => qn(1));
	ff_d2: dff_vhdl port map(d => qn(2), prs => '0', clr => zn, clk => qn(1), q => qstate(2), qn => qn(2));
	ff_d3: dff_vhdl port map(d => qn(3), prs => '0', clr => zn, clk => qn(2), q => qstate(3), qn => qn(3));
	q(0) <= not qstate(0);
	q(1) <= not qstate(1);
	q(2) <= not qstate(2);
	q(3) <= not qstate(3);
end cnt_down_mod16_arch;

// VHDL entity P7_cnt_down_mod10_vhdl, as the project stores it:
library ieee;
use ieee.std_logic_1164.all;

entity P7_cnt_down_mod10_vhdl is
  port(
    clk, z  : in  std_logic;					
    q       : out std_logic_vector(3 downto 0)	
 );
end P7_cnt_down_mod10_vhdl;

architecture cnt_down_mod10_arch of P7_cnt_down_mod10_vhdl is
	signal zn: std_logic;
	signal qn: std_logic_vector(3 downto 0);
	signal qstate: std_logic_vector(3 downto 0);
	signal rst, ff_rst_in, ff_rst_out: std_logic;	
	component dff_vhdl is					
		port
		(
			d, clk, prs, clr	: in  std_logic;	
			q, qn			: out std_logic 	
		);
	end component;	
begin
	zn <= not z;
	ff_rst_in <= not (qstate(0) or (qstate(1) or (qstate(2) or qstate(3))));
	rst <= ((not z) or (ff_rst_out and (qstate(0) and (qstate(1) and (qstate(2) and qstate(3))))));
	ff_d0: dff_vhdl  port map(d => qn(0), prs => rst,       clr => '0',  clk => clk,	  q => qstate(0), qn => qn(0));
	ff_d1: dff_vhdl  port map(d => qn(1), prs => '0',       clr => rst,  clk => qstate(0), q => qstate(1), qn => qn(1));
	ff_d2: dff_vhdl  port map(d => qn(2), prs => '0',       clr => rst,  clk => qstate(1), q => qstate(2), qn => qn(2));
	ff_d3: dff_vhdl  port map(d => qn(3), prs => rst,       clr => '0',  clk => qstate(2), q => qstate(3), qn => qn(3));
	ff_rst: dff_vhdl port map(d => '0',   prs => ff_rst_in, clr => rst,  clk => '0',       q => ff_rst_out);
	q(0) <= qstate(0);
	q(1) <= qstate(1);
	q(2) <= qstate(2);
	q(3) <= qstate(3);
end cnt_down_mod10_arch;

// VHDL entity P8_cnt_down_mod10_alargador_vhdl, as the project stores it:
library ieee;
use ieee.std_logic_1164.all;

entity P8_cnt_down_mod10_alargador_vhdl is
  port(
    clk, z  : in  std_logic;					
    q       : out std_logic_vector(3 downto 0)	
 );
end P8_cnt_down_mod10_alargador_vhdl;

architecture cnt_down_mod10_alargador_arch of P8_cnt_down_mod10_alargador_vhdl is
	signal zn: std_logic;
	signal qn: std_logic_vector(3 downto 0);	
	signal qstate: std_logic_vector(3 downto 0);
	signal rst, ff_rst_in, ff_rst_out, clkn, prs_rst, ff_rst, clr_alargador, clr_aux: std_logic;
	component dff_vhdl is					
		port
		(
			d, clk, prs, clr	: in  std_logic;
			q, qn			: out std_logic
		);
	end component;
begin
	zn <= not z;
	clkn <= not clk;
	rst <= ff_rst_out and (qstate(0) and (qstate(1) and (qstate(2) and qstate(3))));
	ff_rst_in <= not (qstate(0) or (qstate(1) or (qstate(2) or qstate(3))));
	prs_rst <= rst or zn;
	ff_d0:                  dff_vhdl port map(d => qn(0), prs => clr_aux,   clr => '0',    clk => clk,       q => qstate(0), qn => qn(0));
	ff_d1:                  dff_vhdl port map(d => qn(1), prs => '0',       clr => ff_rst, clk => qstate(0), q => qstate(1), qn => qn(1));
	ff_d2:                  dff_vhdl port map(d => qn(2), prs => '0',       clr => ff_rst, clk => qstate(1), q => qstate(2), qn => qn(2));
	ff_d3:                  dff_vhdl port map(d => qn(3), prs => clr_aux,   clr => '0',    clk => qstate(2), q => qstate(3), qn => qn(3));
	ff_reset:               dff_vhdl port map(d => '0',   prs => ff_rst_in, clr => ff_rst, clk => '0',       q => ff_rst_out);
	ff_reset_alargador:     dff_vhdl port map(d => '0',   prs => prs_rst,   clr => clkn,   clk => '0',       q => ff_rst);
	ff_reset_clr_alargador: dff_vhdl port map(d => '0',   prs => zn,        clr => clkn,   clk => '0',       q => clr_alargador);
	clr_aux <= '1' when clr_alargador = '1' else '0';
	q(0) <= qstate(0);
	q(1) <= qstate(1);
	q(2) <= qstate(2);
	q(3) <= qstate(3);
end cnt_down_mod10_alargador_arch;

// VHDL entity P9_cnt_down_mod6_vhdl, as the project stores it:
library ieee;
use ieee.std_logic_1164.all;

entity P9_cnt_down_mod6_vhdl is
  port(
    clk, z  : in  std_logic;					
    q       : out std_logic_vector(3 downto 0)	
 );
end P9_cnt_down_mod6_vhdl;

architecture P9_cnt_down_mod6_arch of P9_cnt_down_mod6_vhdl is
	signal zn: std_logic;
	signal qn: std_logic_vector(3 downto 0);	
	signal qstate: std_logic_vector(3 downto 0);
	signal rst: std_logic; 		
	component dff_vhdl is					
		port
		(
			d, clk, prs, clr	: in  std_logic;	
			q, qn			: out std_logic 	
		);
	end component;
begin
	rst <= ((not z) or (qstate(0) and (qstate(1) and (qstate(2) and qstate(3)))));
	zn <= not z;
	ff_d0: dff_vhdl port map(d => qn(0), prs => rst, clr => '0',  clk => clk,       q => qstate(0), qn => qn(0));
	ff_d1: dff_vhdl port map(d => qn(1), prs => '0', clr => rst, clk => qstate(0), q => qstate(1), qn => qn(1));
	ff_d2: dff_vhdl port map(d => qn(2), prs => rst, clr => '0',  clk => qstate(1), q => qstate(2), qn => qn(2));
	ff_d3: dff_vhdl port map(d => qn(3), prs => '0', clr => rst, clk => qstate(2), q => qstate(3), qn => qn(3));
	q(0) <= qstate(0);
	q(1) <= qstate(1);
	q(2) <= qstate(2);
	q(3) <= qstate(3);
end P9_cnt_down_mod6_arch;

// VHDL entity P10_cnt_down_mod6_alargador_vhdl, as the project stores it:
library ieee;
use ieee.std_logic_1164.all;

entity P10_cnt_down_mod6_alargador_vhdl is
  port(
    clk, z  : in  std_logic;					
    q       : out std_logic_vector(3 downto 0)	
 );
end P10_cnt_down_mod6_alargador_vhdl;

architecture P10_cnt_down_mod6_alargador_arch of P10_cnt_down_mod6_alargador_vhdl is
	signal zn: std_logic;
	signal qn: std_logic_vector(3 downto 0);
	signal qstate: std_logic_vector(3 downto 0);
	signal rst, clkn, prs_rst, ff_rst, clr_alargador, clr_aux: std_logic;
	component dff_vhdl is					
		port
		(
			d, clk, prs, clr	: in  std_logic;	
			q, qn			: out std_logic
		);
	end component;
begin
	zn <= not z;
	clkn <= not clk;
	rst <= (qstate(0) and (qstate(1) and (qstate(2) and qstate(3))));
	prs_rst <= rst or zn;
	ff_d0:                  dff_vhdl port map(d => qn(0), prs => clr_aux, clr => '0',    clk => clk,       q => qstate(0), qn => qn(0));
	ff_d1:                  dff_vhdl port map(d => qn(1), prs => '0',     clr => ff_rst, clk => qstate(0), q => qstate(1), qn => qn(1));
	ff_d2:                  dff_vhdl port map(d => qn(2), prs => clr_aux, clr => '0',    clk => qstate(1), q => qstate(2), qn => qn(2));
	ff_d3:                  dff_vhdl port map(d => qn(3), prs => '0',     clr => ff_rst, clk => qstate(2), q => qstate(3), qn => qn(3));
	ff_rst_alargador:       dff_vhdl port map(d => '0',   prs => prs_rst, clr => clkn,   clk => '0',       q => ff_rst);
	ff_reset_clr_alargador: dff_vhdl port map(d => '0',   prs => zn,      clr => clkn,   clk => '0',       q => clr_alargador);
	clr_aux <= '1' when clr_alargador = '1' else '0';
	q(0) <= qstate(0);
	q(1) <= qstate(1);
	q(2) <= qstate(2);
	q(3) <= qstate(3);
end P10_cnt_down_mod6_alargador_arch;

// VHDL entity P11_cnt_up_down_mod10_vhdl, as the project stores it:
library ieee;
use ieee.std_logic_1164.all;
	
entity P11_cnt_up_down_mod10_vhdl is
	port(
		clk, z, ud	: in  std_logic;					
	    	q       		: out std_logic_vector(3 downto 0);	
	    	co 			: out std_logic
	 );
end P11_cnt_up_down_mod10_vhdl;
	
architecture nt_up_down_mod10_arch of P11_cnt_up_down_mod10_vhdl is
	signal q_up, q_down, qstate_up, qstate_down, qn_up, qn_down: std_logic_vector(3 downto 0);
	signal clk_up, clk_down, clkn_up, clkn_down, rst, zn, reset, ff_rst_in, ff_rst_out, rst_alargador, ff_rst, clr_alargador, clr_aux, prs_rst: std_logic;	
	component dff_vhdl is					-- dff referenciado como dff_vhdl
		port(
			d, clk, prs, clr	: in  std_logic;	-- entradas: dado, clk, preset e clear
			q, qn			: out std_logic 	-- saídas:   q e q invertido
		);
	end component;
begin
	q(0) <= q_up(0) when ud = '0' else q_down(0);
	q(1) <= q_up(1) when ud = '0' else q_down(1);
	q(2) <= q_up(2) when ud = '0' else q_down(2);
	q(3) <= q_up(3) when ud = '0' else q_down(3);
	zn <= not z;
	clk_up <= clk when ud = '0' else '0';
	clk_down <= clk when ud = '1' else '0';
	clkn_up <= not clk_up;
	clkn_down <= not clk_down;
	prs_rst <= (zn or (qstate_up(1) and qstate_up(3)));
	ff_d0_up: dff_vhdl port map(d => qn_up(0), prs => '0', clr => clr_aux, clk => clk_up,   q => qstate_up(0), qn => qn_up(0));
	ff_d1_up: dff_vhdl port map(d => qn_up(1), prs => '0', clr => clr_aux, clk => qn_up(0), q => qstate_up(1), qn => qn_up(1));
	ff_d2_up: dff_vhdl port map(d => qn_up(2), prs => '0', clr => clr_aux, clk => qn_up(1), q => qstate_up(2), qn => qn_up(2));
	ff_d3_up: dff_vhdl port map(d => qn_up(3), prs => '0', clr => clr_aux, clk => qn_up(2), q => qstate_up(3), qn => qn_up(3));
	ff_rst_up: dff_vhdl port map(d => '0', prs => prs_rst, clr => clkn_up, clk => '0', q => clr_aux);
	q_up(0) <= qstate_up(0);
	q_up(1) <= qstate_up(1);
	q_up(2) <= qstate_up(2);
	q_up(3) <= qstate_up(3);
	reset <= ff_rst_out and (qstate_down(0) and (qstate_down(1) and (qstate_down(2) and qstate_down(3))));
	ff_rst_in <= not (qstate_down(0) or (qstate_down(1) or (qstate_down(2) or qstate_down(3))));
	rst_alargador <= reset or zn;
	ff_d0_down: dff_vhdl port map(d => qn_down(0), prs => rst, clr => '0', clk => clk_down, q => qstate_down(0), qn => qn_down(0));
	ff_d1_down: dff_vhdl port map(d => qn_down(1), prs => '0', clr => ff_rst, clk => qstate_down(0), q => qstate_down(1), qn => qn_down(1));
	ff_d2_down: dff_vhdl port map(d => qn_down(2), prs => '0', clr => ff_rst, clk => qstate_down(1), q => qstate_down(2), qn => qn_down(2));
	ff_d3_down: dff_vhdl port map(d => qn_down(3), prs => rst, clr => '0', clk => qstate_down(2), q => qstate_down(3), qn => qn_down(3));
	ff_rst_down: dff_vhdl port map(d => '0', prs => ff_rst_in, clr => ff_rst, clk => '0', q => ff_rst_out);
	ff_rst_alargador_down: dff_vhdl   port map(d => '0', prs => rst_alargador, clr => clkn_down, clk => '0', q => ff_rst);
	ff_rst_alargador_clr_down: dff_vhdl port map(d => '0', prs => zn, clr => clkn_down, clk => '0', q => clr_alargador);
	rst <= '1' when clr_alargador = '1' else '0';
	q_down(0) <= qstate_down(0);
	q_down(1) <= qstate_down(1);
	q_down(2) <= qstate_down(2);
	q_down(3) <= qstate_down(3);
	co <= clr_aux when ud = '0' else ff_rst;
end nt_up_down_mod10_arch;

// VHDL entity P12_cnt_up_down_mod6_vhdl, as the project stores it:
library ieee;
use ieee.std_logic_1164.all;

entity P12_cnt_up_down_mod6_vhdl is
	port(
    		clk, z, ud	: in  std_logic;					
    		q       		: out std_logic_vector(3 downto 0)	
	 );
end P12_cnt_up_down_mod6_vhdl;

architecture P12_cnt_up_down_mod6_arch of P12_cnt_up_down_mod6_vhdl is
	signal q_up, q_down, qstate_up, qstate_down, qn_up, qn_down: std_logic_vector(3 downto 0);
	signal clk_up, clk_down, clkn_up, clkn_down, rst, zn, reset, ff_rst_in, ff_rst_out, rst_alargador, ff_rst, clr_alargador, clr_aux, prs_rst: std_logic;
	component dff_vhdl is					
		port(
			d, clk, prs, clr	: in  std_logic;	
			q, qn			: out std_logic
		);
	end component;
begin
	q(0) <= q_up(0) when ud = '0' else q_down(0);
	q(1) <= q_up(1) when ud = '0' else q_down(1);
	q(2) <= q_up(2) when ud = '0' else q_down(2);
	q(3) <= q_up(3) when ud = '0' else q_down(3);
	zn <= not z;
	clk_up <= clk when ud = '0';
	clk_down <= clk when ud = '1';
	clkn_up <= not clk_up;
	clkn_down <= not clk_down;
	prs_rst <= (zn or (qstate_up(1) and qstate_up(2)));
	ff_d0_up:  dff_vhdl port map(d => qn_up(0), prs => '0',     clr => clr_aux, clk => clk_up,   q => qstate_up(0), qn => qn_up(0));
	ff_d1_up:  dff_vhdl port map(d => qn_up(1), prs => '0',     clr => clr_aux, clk => qn_up(0), q => qstate_up(1), qn => qn_up(1));
	ff_d2_up:  dff_vhdl port map(d => qn_up(2), prs => '0',     clr => clr_aux, clk => qn_up(1), q => qstate_up(2), qn => qn_up(2));
	ff_d3_up:  dff_vhdl port map(d => qn_up(3), prs => '0',     clr => clr_aux, clk => qn_up(2), q => qstate_up(3), qn => qn_up(3));
	ff_rst_up: dff_vhdl port map(d => '0',      prs => prs_rst, clr => clkn_up, clk => '0',      q => clr_aux);
	q_up(0) <= qstate_up(0);
	q_up(1) <= qstate_up(1);
	q_up(2) <= qstate_up(2);
	q_up(3) <= qstate_up(3);
	reset <= (qstate_down(0) and (qstate_down(1) and (qstate_down(2) and qstate_down(3))));
	rst_alargador <= reset or zn;
	ff_d0_down: dff_vhdl port map(d => qn_down(0), prs => rst, clr => '0',    clk => clk_down,       q => qstate_down(0), qn => qn_down(0));
	ff_d1_down: dff_vhdl port map(d => qn_down(1), prs => '0', clr => ff_rst, clk => qstate_down(0), q => qstate_down(1), qn => qn_down(1));
	ff_d2_down: dff_vhdl port map(d => qn_down(2), prs => rst, clr => '0', clk => qstate_down(1), q => qstate_down(2), qn => qn_down(2));
	ff_d3_down: dff_vhdl port map(d => qn_down(3), prs => '0', clr => ff_rst,    clk => qstate_down(2), q => qstate_down(3), qn => qn_down(3));
	ff_rst_alargador_down: dff_vhdl port map(d => '0', prs => rst_alargador, clr => clkn_down, clk => '0', q => ff_rst);
	ff_rst_clr_alargador_down: dff_vhdl port map(d => '0', prs => zn, clr => clkn_down, clk => '0', q => clr_alargador);
	rst <= '1' when clr_alargador = '1' else '0';
	q_down(0) <= qstate_down(0);
	q_down(1) <= qstate_down(1);
	q_down(2) <= qstate_down(2);
	q_down(3) <= qstate_down(3);
end P12_cnt_up_down_mod6_arch;

// VHDL entity P13_cnt_up_down_mod60_vhdl, as the project stores it:
library ieee;
use ieee.std_logic_1164.all;

entity P13_cnt_up_down_mod60_vhdl is
	port(
    		clk, z, ud, sst  	: in  std_logic;					
    		qu, qd       		: out std_logic_vector(3 downto 0)	

 );
end P13_cnt_up_down_mod60_vhdl;

architecture cnt_up_down_mod60_arch of P13_cnt_up_down_mod60_vhdl is
	signal ff_rst_in, ff_rst_out, qo: std_logic;
	signal q_up_m10, q_down_m10, qstate_up_m10, qstate_down_m10, qn_up_m10, qn_down_m10: std_logic_vector(3 downto 0);
	signal clk_up_m10, clk_down_m10, clkn_up_m10, clkn_down_m10, rst_m10, zn_m10, reset_m10, rst_alargador_m10, ff_rst_m10, clr_alargador_m10, clr_aux_m10, prs_rst_m10: std_logic;
	signal q_up_m6, q_down_m6, qstate_up_m6, qstate_down_m6, qn_up_m6, qn_down_m6: std_logic_vector(3 downto 0);
	signal clk_up_m6, clk_down_m6, clkn_up_m6, clkn_down_m6, rst_m6, zn_m6, reset_m6, rst_alargador_m6, ff_rst_m6, clr_alargador_m6, clr_aux_m6, prs_rst_m6: std_logic;
	component dff_vhdl is					
		port(
			d, clk, prs, clr	: in  std_logic;	
			q, qn			: out std_logic 	
		);
	end component;	
begin
	qu(0) <= q_up_m10(0) when ud = '0' else q_down_m10(0);
	qu(1) <= q_up_m10(1) when ud = '0' else q_down_m10(1);
	qu(2) <= q_up_m10(2) when ud = '0' else q_down_m10(2);
	qu(3) <= q_up_m10(3) when ud = '0' else q_down_m10(3);
	zn_m10 <= not z;
	clk_up_m10 <= clk when ud = '0';
	clk_down_m10 <= clk when ud = '1';
	clkn_up_m10 <= not clk_up_m10;
	clkn_down_m10 <= not clk_down_m10;
	prs_rst_m10 <= (zn_m10 or (qstate_up_m10(1) and qstate_up_m10(3)));
	ff_d0_up_m10: dff_vhdl port map(d => qn_up_m10(0), prs => '0', clr => clr_aux_m10, clk => clk_up_m10,   q => qstate_up_m10(0), qn => qn_up_m10(0));
	ff_d1_up_m10: dff_vhdl port map(d => qn_up_m10(1), prs => '0', clr => clr_aux_m10, clk => qn_up_m10(0), q => qstate_up_m10(1), qn => qn_up_m10(1));
	ff_d2_up_m10: dff_vhdl port map(d => qn_up_m10(2), prs => '0', clr => clr_aux_m10, clk => qn_up_m10(1), q => qstate_up_m10(2), qn => qn_up_m10(2));
	ff_d3_up_m10: dff_vhdl port map(d => qn_up_m10(3), prs => '0', clr => clr_aux_m10, clk => qn_up_m10(2), q => qstate_up_m10(3), qn => qn_up_m10(3));
	ff_rst_up_m10: dff_vhdl port map(d => '0', prs => prs_rst_m10, clr => clkn_up_m10, clk => '0', q => clr_aux_m10);
	q_up_m10(0) <= qstate_up_m10(0);
	q_up_m10(1) <= qstate_up_m10(1);
	q_up_m10(2) <= qstate_up_m10(2);
	q_up_m10(3) <= qstate_up_m10(3);
	reset_m10 <= ff_rst_out and (qstate_down_m10(0) and (qstate_down_m10(1) and (qstate_down_m10(2) and qstate_down_m10(3))));
	ff_rst_in <= not (qstate_down_m10(0) or (qstate_down_m10(1) or (qstate_down_m10(2) or qstate_down_m10(3))));
	rst_alargador_m10 <= reset_m10 or zn_m10;
	ff_d0_down_m10: dff_vhdl port map(d => qn_down_m10(0), prs => rst_m10, clr => '0', clk => clk_down_m10, q => qstate_down_m10(0), qn => qn_down_m10(0));
	ff_d1_down_m10: dff_vhdl port map(d => qn_down_m10(1), prs => '0', clr => ff_rst_m10, clk => qstate_down_m10(0), q => qstate_down_m10(1), qn => qn_down_m10(1));
	ff_d2_down_m10: dff_vhdl port map(d => qn_down_m10(2), prs => '0', clr => ff_rst_m10, clk => qstate_down_m10(1), q => qstate_down_m10(2), qn => qn_down_m10(2));
	ff_d3_down_m10: dff_vhdl port map(d => qn_down_m10(3), prs => rst_m10, clr => '0', clk => qstate_down_m10(2), q => qstate_down_m10(3), qn => qn_down_m10(3));
	ff_rst_down_m10: dff_vhdl port map(d => '0', prs => ff_rst_in, clr => ff_rst_m10, clk => '0', q => ff_rst_out);
	ff_rst_alargador_down_m10: dff_vhdl port map(d => '0', prs => rst_alargador_m10, clr => clkn_down_m10, clk => '0', q => ff_rst_m10);
	ff_rst_alargador_clr_down_m10: dff_vhdl port map(d => '0', prs => zn_m10, clr => clkn_down_m10, clk => '0', q => clr_alargador_m10);
	rst_m10 <= '1' when clr_alargador_m10 = '1' else '0';
	q_down_m10(0) <= qstate_down_m10(0);
	q_down_m10(1) <= qstate_down_m10(1);
	q_down_m10(2) <= qstate_down_m10(2);
	q_down_m10(3) <= qstate_down_m10(3);
	qo <= clr_aux_m10 when ud = '0' else ff_rst_m10;
	qd(0) <= q_up_m6(0) when ud = '0' else q_down_m6(0);
	qd(1) <= q_up_m6(1) when ud = '0' else q_down_m6(1);
	qd(2) <= q_up_m6(2) when ud = '0' else q_down_m6(2);
	qd(3) <= q_up_m6(3) when ud = '0' else q_down_m6(3);
	zn_m6 <= not z;
	clk_up_m6 <= qo when ud = '0';
	clk_down_m6 <= qo when ud = '1';
	clkn_up_m6 <= not clk_up_m6;
	clkn_down_m6 <= not clk_down_m6;
	prs_rst_m6 <= (zn_m6 or (qstate_up_m6(1) and qstate_up_m6(3)));
	ff_d0_up_m6: dff_vhdl port map(d => qn_up_m6(0), prs => '0', clr => clr_aux_m6, clk => clk_up_m6,   q => qstate_up_m6(0), qn => qn_up_m6(0));
	ff_d1_up_m6: dff_vhdl port map(d => qn_up_m6(1), prs => '0', clr => clr_aux_m6, clk => qn_up_m6(0), q => qstate_up_m6(1), qn => qn_up_m6(1));
	ff_d2_up_m6: dff_vhdl port map(d => qn_up_m6(2), prs => '0', clr => clr_aux_m6, clk => qn_up_m6(1), q => qstate_up_m6(2), qn => qn_up_m6(2));
	ff_d3_up_m6: dff_vhdl port map(d => qn_up_m6(3), prs => '0', clr => clr_aux_m6, clk => qn_up_m6(2), q => qstate_up_m6(3), qn => qn_up_m6(3));
	ff_rst_up_m6: dff_vhdl port map(d => '0', prs => prs_rst_m6, clr => clkn_up_m6, clk => '0', q => clr_aux_m6);
	q_up_m6(0) <= qstate_up_m6(0);
	q_up_m6(1) <= qstate_up_m6(1);
	q_up_m6(2) <= qstate_up_m6(2);
	q_up_m6(3) <= qstate_up_m6(3);
	reset_m6 <= qstate_down_m6(0) and (qstate_down_m6(1) and (qstate_down_m6(2) and qstate_down_m6(3)));
	rst_alargador_m6 <= reset_m6 or zn_m6;
	ff_d0_down_m6: dff_vhdl port map(d => qn_down_m6(0), prs => rst_m6, clr => '0', clk => clk_down_m6, q => qstate_down_m6(0), qn => qn_down_m6(0));
	ff_d1_down_m6: dff_vhdl port map(d => qn_down_m6(1), prs => '0', clr => ff_rst_m6, clk => qstate_down_m6(0), q => qstate_down_m6(1), qn => qn_down_m6(1));
	ff_d2_down_m6: dff_vhdl port map(d => qn_down_m6(2), prs => rst_m6, clr => '0', clk => qstate_down_m6(1), q => qstate_down_m6(2), qn => qn_down_m6(2));
	ff_d3_down_m6: dff_vhdl port map(d => qn_down_m6(3), prs => '0', clr => ff_rst_m6, clk => qstate_down_m6(2), q => qstate_down_m6(3), qn => qn_down_m6(3));
	ff_rst_alargador_down_m6: dff_vhdl port map(d => '0', prs => rst_alargador_m6, clr => clkn_down_m6, clk => '0', q => ff_rst_m6);
	ff_rst_alargador_clr_down_m6: dff_vhdl port map(d => '0', prs => zn_m6, clr => clkn_down_m6, clk => '0', q => clr_alargador_m6);
	rst_m6 <= '1' when clr_alargador_m6 = '1' else '0';
	q_down_m6(0) <= qstate_down_m6(0);
	q_down_m6(1) <= qstate_down_m6(1);
	q_down_m6(2) <= qstate_down_m6(2);
	q_down_m6(3) <= qstate_down_m6(3);
end cnt_up_down_mod60_arch;

// VHDL entity P14_cnt_up_down_mod60_vhdl, as the project stores it:
library ieee;
use ieee.std_logic_1164.all;

entity P14_cnt_up_down_mod60_vhdl is
	port(
		clk, z, ud, sst		: in  std_logic;	
		qu_7s, qd_7s       	: out std_logic_vector(6 downto 0);		
		clk_in, clk_out		: out std_logic							
);
end P14_cnt_up_down_mod60_vhdl;

architecture cnt_up_down_mod60_2_vhdl of P14_cnt_up_down_mod60_vhdl is
	signal q_up_m10, q_down_m10, qstate_up_m10, qstate_down_m10, qn_up_m10, qn_down_m10: std_logic_vector(3 downto 0);
	signal clk_up_m10, clk_down_m10, clkn_up_m10, clkn_down_m10, zn_m10, reset_m10, rst_alargador_m10, ff_rst_m10, clr_alargador_m10, clr_aux_m10, prs_rst_m10: std_logic;
	signal q_up_m6, q_down_m6, qstate_up_m6, qstate_down_m6, qn_up_m6, qn_down_m6: std_logic_vector(3 downto 0);
	signal clk_up_m6, clk_down_m6, clkn_up_m6, clkn_down_m6, zn_m6, reset_m6, rst_alargador_m6, ff_rst_m6, clr_alargador_m6, clr_aux_m6, prs_rst_m6: std_logic;
	signal qu, qd: std_logic_vector(3 downto 0);
	signal qo, ff_rst_in, ff_rst_out, reset_u, reset_d, clk_anti_repique, div_out, clk_div_debounce_out, ff_sst_q_out, ff_sst_qn_out, clk_debounce: std_logic;
	component dff_vhdl is				
		port
		(
			d, clk, prs, clr	: in  std_logic;	
			q, qn				: out std_logic 	
		);
	end component;
	component divider is
	port(
		clk_in					: in  std_logic;	
		clk_out_1, clk_out_2	: out std_logic	
	);
	end component;
	component debounce_v1 is
	port(
		clk, button	: in  std_logic;    
		result  	: out std_logic
	);
	end component;
begin
	clk_out <= div_out;
	clk_in <= not div_out;
	div : divider port map(clk_in => clk, clk_out_1 => clk_debounce, clk_out_2 => div_out);
	deb : debounce_v1 port map(clk => clk_debounce, button => sst, result => clk_anti_repique);
	ff_sst: dff_vhdl port map(d => ff_sst_qn_out, prs => '0', clr => zn_m10, clk => clk_anti_repique, q => ff_sst_q_out, qn => ff_sst_qn_out);
	clk_div_debounce_out <= div_out and ff_sst_q_out;
	qu(0) <= q_up_m10(0) when ud = '0' else q_down_m10(0);
	qu(1) <= q_up_m10(1) when ud = '0' else q_down_m10(1);
	qu(2) <= q_up_m10(2) when ud = '0' else q_down_m10(2);
	qu(3) <= q_up_m10(3) when ud = '0' else q_down_m10(3);
	zn_m10 <= not z;
	clk_up_m10 <= clk_div_debounce_out when ud = '0';
	clk_down_m10 <= clk_div_debounce_out when ud = '1';
	clkn_up_m10 <= not clk_up_m10;
	clkn_down_m10 <= not clk_down_m10;
	prs_rst_m10 <= (zn_m10 or (qstate_up_m10(1) and qstate_up_m10(3)));
	ff_d0_up_m10: dff_vhdl port map(d => qn_up_m10(0), prs => '0', clr => clr_aux_m10, clk => clk_up_m10,   q => qstate_up_m10(0), qn => qn_up_m10(0));
	ff_d1_up_m10: dff_vhdl port map(d => qn_up_m10(1), prs => '0', clr => clr_aux_m10, clk => qn_up_m10(0), q => qstate_up_m10(1), qn => qn_up_m10(1));
	ff_d2_up_m10: dff_vhdl port map(d => qn_up_m10(2), prs => '0', clr => clr_aux_m10, clk => qn_up_m10(1), q => qstate_up_m10(2), qn => qn_up_m10(2));
	ff_d3_up_m10: dff_vhdl port map(d => qn_up_m10(3), prs => '0', clr => clr_aux_m10, clk => qn_up_m10(2), q => qstate_up_m10(3), qn => qn_up_m10(3));
	ff_reset_up_m10: dff_vhdl port map(d => '0', prs => prs_rst_m10, clr => clkn_up_m10, clk => '0', q => clr_aux_m10);
	q_up_m10(0) <= qstate_up_m10(0);
	q_up_m10(1) <= qstate_up_m10(1);
	q_up_m10(2) <= qstate_up_m10(2);
	q_up_m10(3) <= qstate_up_m10(3);
	reset_m10 <= ff_rst_out and (qstate_down_m10(0) and (qstate_down_m10(1) and (qstate_down_m10(2) and qstate_down_m10(3))));
	ff_rst_in <= not (qstate_down_m10(0) or (qstate_down_m10(1) or (qstate_down_m10(2) or qstate_down_m10(3))));
	rst_alargador_m10 <= reset_m10 or zn_m10;
	ff_d0_down_m10: dff_vhdl port map(d => qn_down_m10(0), prs => reset_u, clr => '0', clk => clk_down_m10, q => qstate_down_m10(0), qn => qn_down_m10(0));
	ff_d1_down_m10: dff_vhdl port map(d => qn_down_m10(1), prs => '0', clr => ff_rst_m10, clk => qstate_down_m10(0), q => qstate_down_m10(1), qn => qn_down_m10(1));
	ff_d2_down_m10: dff_vhdl port map(d => qn_down_m10(2), prs => '0', clr => ff_rst_m10, clk => qstate_down_m10(1), q => qstate_down_m10(2), qn => qn_down_m10(2));
	ff_d3_down_m10: dff_vhdl port map(d => qn_down_m10(3), prs => reset_u, clr => '0', clk => qstate_down_m10(2), q => qstate_down_m10(3), qn => qn_down_m10(3));
	ff_reset_down_m10: dff_vhdl port map(d => '0', prs => ff_rst_in, clr => ff_rst_m10, clk => '0', q => ff_rst_out);
	ff_reset_alargador_down_m10: dff_vhdl port map(d => '0', prs => rst_alargador_m10, clr => clkn_down_m10, clk => '0', q => ff_rst_m10);
	reset_u <= '1' when ff_rst_m10 = '1' else '0';
	q_down_m10(0) <= qstate_down_m10(0);
	q_down_m10(1) <= qstate_down_m10(1);
	q_down_m10(2) <= qstate_down_m10(2);
	q_down_m10(3) <= qstate_down_m10(3);
	qo <= clr_aux_m10 when ud = '0' else ff_rst_m10;
	qd(0) <= q_up_m6(0) when ud = '0' else q_down_m6(0);
	qd(1) <= q_up_m6(1) when ud = '0' else q_down_m6(1);
	qd(2) <= q_up_m6(2) when ud = '0' else q_down_m6(2);
	qd(3) <= q_up_m6(3) when ud = '0' else q_down_m6(3);
	zn_m6 <= not z;
	clk_up_m6 <= qo when ud = '0';
	clk_down_m6 <= qo when ud = '1';
	clkn_up_m6 <= not clk_up_m6;
	clkn_down_m6 <= not clk_down_m6;
	prs_rst_m6 <= (zn_m6 or (qstate_up_m6(1) and qstate_up_m6(2)));
	ff_d0_up_m6: dff_vhdl port map(d => qn_up_m6(0), prs => '0', clr => clr_aux_m6, clk => clk_up_m6,   q => qstate_up_m6(0), qn => qn_up_m6(0));
	ff_d1_up_m6: dff_vhdl port map(d => qn_up_m6(1), prs => '0', clr => clr_aux_m6, clk => qn_up_m6(0), q => qstate_up_m6(1), qn => qn_up_m6(1));
	ff_d2_up_m6: dff_vhdl port map(d => qn_up_m6(2), prs => '0', clr => clr_aux_m6, clk => qn_up_m6(1), q => qstate_up_m6(2), qn => qn_up_m6(2));
	ff_d3_up_m6: dff_vhdl port map(d => qn_up_m6(3), prs => '0', clr => clr_aux_m6, clk => qn_up_m6(2), q => qstate_up_m6(3), qn => qn_up_m6(3));
	ff_reset_up_m6: dff_vhdl port map(d => '0', prs => prs_rst_m6, clr => clkn_up_m6, clk => '0', q => clr_aux_m6);
	q_up_m6(0) <= qstate_up_m6(0);
	q_up_m6(1) <= qstate_up_m6(1);
	q_up_m6(2) <= qstate_up_m6(2);
	q_up_m6(3) <= qstate_up_m6(3);
	reset_m6 <= qstate_down_m6(0) and (qstate_down_m6(1) and (qstate_down_m6(2) and qstate_down_m6(3)));
	rst_alargador_m6 <= reset_m6 or zn_m6;
	ff_d0_down_m6: dff_vhdl port map(d => qn_down_m6(0), prs => reset_d, clr => '0', clk => clk_down_m6, q => qstate_down_m6(0), qn => qn_down_m6(0));
	ff_d1_down_m6: dff_vhdl port map(d => qn_down_m6(1), prs => '0', clr => ff_rst_m6, clk => qstate_down_m6(0), q => qstate_down_m6(1), qn => qn_down_m6(1));
	ff_d2_down_m6: dff_vhdl port map(d => qn_down_m6(2), prs => reset_d, clr => '0', clk => qstate_down_m6(1), q => qstate_down_m6(2), qn => qn_down_m6(2));
	ff_d3_down_m6: dff_vhdl port map(d => qn_down_m6(3), prs => '0', clr => ff_rst_m6, clk => qstate_down_m6(2), q => qstate_down_m6(3), qn => qn_down_m6(3));
	ff_reset_alargador_down_m6: dff_vhdl port map(d => '0', prs => rst_alargador_m6, clr => clkn_down_m6, clk => '0', q => ff_rst_m6);
	reset_d <= '1' when ff_rst_m6 = '1' else '0';
	q_down_m6(0) <= qstate_down_m6(0);
	q_down_m6(1) <= qstate_down_m6(1);
	q_down_m6(2) <= qstate_down_m6(2);
	q_down_m6(3) <= qstate_down_m6(3);
	with qu select
		qu_7s <=    "1111110" when "0000",
                    "0110000" when "0001",
                    "1101101" when "0010",
                    "1111001" when "0011",
                    "0110011" when "0100",
                    "1011011" when "0101",
                    "1011111" when "0110",
                    "1110000" when "0111",
                    "1111111" when "1000",
                    "1110011" when "1001",
                    "1110111" when "1010",
                    "0011111" when "1011",
                    "1001110" when "1100",
                    "0111101" when "1101",
                    "1111001" when "1110",
                    "0111100" when "1111",
                    "0000000" when others;
	with qd select
		qd_7s <=    "1111110" when "0000",
                    "0110000" when "0001",
                    "1101101" when "0010",
                    "1111001" when "0011",
                    "0110011" when "0100",
                    "1011011" when "0101",
                    "1011111" when "0110",
                    "1110000" when "0111",
                    "1111111" when "1000",
                    "1110011" when "1001",
                    "1110111" when "1010",
                    "0011111" when "1011",
                    "1001110" when "1100",
                    "0111101" when "1101",
                    "1111001" when "1110",
                    "0111100" when "1111",
                    "0000000" when others;
end cnt_up_down_mod60_2_vhdl;
