// Logisim project L7.circ as structural Verilog
module main (
  input  SEQ
);

  wire and_1_out, CLK_out, RST_out;
  wire [2:0] bloco_comb_mux_8_1_prx_est, bloco_sequencial_1_est_prs;
  wire [3:0] detetor_seq_1_est_out, detetor_seq_1_res_out, multiplexer_1_out;

  Clock CLK (.out(CLK_out));
  Button RST (.out(RST_out));
  Bloco_Comb_mux_8 bloco_comb_mux_8_1 (
    .SEQ_IN(SEQ), .EST_PRS(bloco_sequencial_1_est_prs), .PRX_EST(bloco_comb_mux_8_1_prx_est));
  Bloco_sequencial bloco_sequencial_1 (
    .PRX_EST(bloco_comb_mux_8_1_prx_est), .CLK(CLK_out), .RST(RST_out), .EST_PRS(bloco_sequencial_1_est_prs));
  Detetor_seq detetor_seq_1 (
    .rst(RST_out), .seq_in(SEQ), .clock(CLK_out), .res_out(detetor_seq_1_res_out),
    .est_out(detetor_seq_1_est_out));
  seq_compr_vari vhdl ();  // open: rst, seq_in, clock, res_out, est_out
  Hex_Digit_Display hex_digit_display_1 (.value(multiplexer_1_out));  // open: dp
  Hex_Digit_Display hex_digit_display_2 (.value({1'b0, bloco_sequencial_1_est_prs}));  // open: dp
  Multiplexer #(.width(4)) multiplexer_1 (.in0(4'b0000), .in1(4'b0001), .out(multiplexer_1_out), .sel(and_1_out));
  and and_1 (and_1_out, ~bloco_sequencial_1_est_prs[0], bloco_sequencial_1_est_prs[1], bloco_sequencial_1_est_prs[2]);  // AND_Gate
  Hex_Digit_Display hex_digit_display_3 (.value(detetor_seq_1_res_out));  // open: dp
  Hex_Digit_Display hex_digit_display_4 (.value(detetor_seq_1_est_out));  // open: dp
endmodule

module Bloco_sequencial (
  input  [2:0] PRX_EST,
  input  CLK,
  input  RST,
  output [2:0] EST_PRS
);

  Register #(.width(3)) register_1 (.D(PRX_EST), .clk(CLK), .Q(EST_PRS), .clr(RST));  // open: en
endmodule

module Bloco_Comb_mux_8 (
  input  SEQ_IN,
  input  [2:0] EST_PRS,
  output [2:0] PRX_EST
);

  wire [0:0] not_1_out;

  not not_1 (not_1_out[0], SEQ_IN);
  Multiplexer #(.select(3), .width(3)) multiplexer_1 (
    .in0({2'b00, not_1_out[0]}), .in1({1'b0, SEQ_IN, 1'b0}), .in2({1'b0, {2{not_1_out[0]}}}),
    .in3({not_1_out[0], 2'b00}), .in4({SEQ_IN, 1'b0, SEQ_IN}), .in5({{2{not_1_out[0]}}, 1'b0}), .in6(3'b110),
    .in7(3'b000), .out(PRX_EST), .sel(EST_PRS));
endmodule

module teste (
  input  SEQ,
  input  in_2
);

  wire and_1_out, button_1_out, CLK_out, clock_1_out, RST_out;
  wire [2:0] bloco_comb_mux_8_1_prx_est, bloco_sequencial_1_est_prs;
  wire [3:0] detetor_seq_1_est_out, detetor_seq_1_res_out, multiplexer_1_out;

  Button RST (.out(RST_out));
  Clock CLK (.out(CLK_out));
  Hex_Digit_Display hex_digit_display_1 (.value(detetor_seq_1_res_out));  // open: dp
  Detetor_seq detetor_seq_1 (
    .rst(RST_out), .seq_in(SEQ), .clock(CLK_out), .res_out(detetor_seq_1_res_out),
    .est_out(detetor_seq_1_est_out));
  Hex_Digit_Display hex_digit_display_2 (.value(detetor_seq_1_est_out));  // open: dp
  Clock clock_1 (.out(clock_1_out));
  Button button_1 (.out(button_1_out));
  Bloco_Comb_mux_8 bloco_comb_mux_8_1 (
    .SEQ_IN(in_2), .EST_PRS(bloco_sequencial_1_est_prs), .PRX_EST(bloco_comb_mux_8_1_prx_est));
  Bloco_sequencial bloco_sequencial_1 (
    .PRX_EST(bloco_comb_mux_8_1_prx_est), .CLK(clock_1_out), .RST(button_1_out),
    .EST_PRS(bloco_sequencial_1_est_prs));
  Hex_Digit_Display hex_digit_display_3 (.value(multiplexer_1_out));  // open: dp
  Hex_Digit_Display hex_digit_display_4 (.value({1'b0, bloco_sequencial_1_est_prs}));  // open: dp
  Multiplexer #(.width(4)) multiplexer_1 (.in0(4'b0000), .in1(4'b0001), .out(multiplexer_1_out), .sel(and_1_out));
  and and_1 (and_1_out, ~bloco_sequencial_1_est_prs[0], bloco_sequencial_1_est_prs[1], bloco_sequencial_1_est_prs[2]);  // AND_Gate
endmodule

// VHDL entity seq_compr_vari, as the project stores it:
library ieee;
use ieee.std_logic_1164.all;
use ieee.numeric_std.all;

entity seq_compr_vari is
	generic(
		bits: natural := 5; 
		seq_to_det: integer := 19
	);
	port(
		rst, seq_in, clock	:	in 	std_logic;
		res_out, est_out	:	out 	std_logic_vector(3 downto 0)
	);
end seq_compr_vari;

architecture detetor of seq_compr_vari is
	constant seq: std_logic_vector(bits-1 downto 0) := std_logic_vector(to_unsigned(seq_to_det, bits));
	signal stat_prs, prx_stat: integer range 0 to bits;
begin
	seq_proc: process(clock, rst)
	begin
		if rst = '1' then stat_prs <= 0;
--		if rst = '0' then stat_prs <= 0;
		elsif clock = '1' and clock 'event then
			stat_prs <= prx_stat;
		end if;
	end process seq_proc;
	comb_proc: process(stat_prs, seq_in)
	variable idx_seq: integer;
	begin
		idx_seq := bits - 1 - stat_prs;
		if stat_prs /= bits then
			if seq_in = seq(idx_seq) then
				prx_stat <= stat_prs + 1;
			else
				prx_stat <= 0;
			end if;
		else
			prx_stat <= bits;
		end if;
		est_out <= std_logic_vector(to_unsigned(stat_prs, est_out'length));
		case stat_prs is
			when bits 	=> res_out <= X"1";
			when others	=> res_out <= X"0";
		end case;
	end process comb_proc;
end detetor;

// VHDL entity Detetor_seq, as the project stores it:
library ieee;
use ieee.std_logic_1164.all;
use ieee.numeric_std.all;

entity Detetor_seq is
	port(
		rst, seq_in, clock	:	in std_logic;
		res_out, est_out	:	out std_logic_vector(3 downto 0)
	);
end Detetor_seq;

architecture detetor of Detetor_seq is
component Seq_compr_vari_vhdl is
	generic(bits: natural := 6; seq_to_det: integer := 18);
	port(
		rst, seq_in, clock	:	in std_logic;
		res_out, est_out	:	out std_logic_vector(3 downto 0)
	);
end component;

begin
	det: Seq_compr_vari_vhdl	generic map(	bits			=> 6,
									seq_to_det	=> 18)
						port map(		rst			=> rst,
									seq_in		=> seq_in,
									clock		=> clock,
									res_out		=> res_out,
									est_out		=> est_out);
end detetor;

// VHDL entity seq_compr_fixo, as the project stores it:
library ieee;
use ieee.std_logic_1164.all;
use ieee.numeric_std.all;

entity seq_compr_fixo is
	generic(iseq: integer := 18);
	port(
		rst, seq_in, clock	:	in	std_logic;
		res_out, est_out	:	out	std_logic_vector(3 downto 0)
	);
end seq_compr_fixo;

architecture detetor of seq_compr_fixo is

type estado is (A, B, C, D, E, F, G);
	constant seq: std_logic_vector(5 downto 0):=std_logic_vector(to_unsigned(iseq, 6));
	signal estado_prs, prx_estado: estado;
	attribute enum_enconding: string;
	attribute enum_enconding of estado: type is "sequential";

begin

	seq_proc: process(clock, rst)
	begin
		if rst = '1' then estado_prs <= A;
		elsif clock = '1' and clock'event then
			estado_prs <= prx_estado;
		end if;
	end process seq_proc;
	
	comb_proc: process(estado_prs, seq_in)
	variable idx_est, idx_seq: integer;
	begin
		idx_est := estado'pos(estado_prs);
		idx_seq := seq'left - idx_est;
		if estado_prs /= estado'right then
			if seq_in = seq(idx_seq) then
				prx_estado <= estado'val(idx_est + 1);
			else
				prx_estado <= estado'left;
			end if;
		else
			prx_estado <= estado'right;
		end if;
		est_out <= std_logic_vector(to_unsigned(idx_est, est_out'length));
		case estado_prs is
			when estado'right	=> res_out <= X"1";
			when others		=> res_out <= X"0";
		end case;
	end process comb_proc;
	
end detetor;
